// Logisim project 50logic_circuit_all_50.circ as structural Verilog: 50 circuits, main circuit 01_1x4_Demultiplexer
module _01_1x4_Demultiplexer (
  input  D,
  input  S1,
  input  S0,
  output Y0,
  output Y1,
  output Y2,
  output Y3
);

  wire not_1_out, not_2_out;

  not not_1 (not_1_out, S1);
  not not_2 (not_2_out, S0);
  and and_1 (Y0, not_1_out, not_2_out, D);
  and and_2 (Y1, not_1_out, S0, D);
  and and_3 (Y2, S1, not_2_out, D);
  and and_4 (Y3, S1, S0, D);

  // Notes on the sheet:
  //   1. 1x4 Demultiplexer
  //   Y0=~S1.~S0.D, Y1=~S1.S0.D, Y2=S1.~S0.D, Y3=S1.S0.D
endmodule

module _02_2x4_Decoder (
  input  A1,
  input  A0,
  output Y0,
  output Y1,
  output Y2,
  output Y3
);

  wire not_1_out, not_2_out;

  not not_1 (not_1_out, A1);
  not not_2 (not_2_out, A0);
  and and_1 (Y0, not_1_out, not_2_out);
  and and_2 (Y1, not_1_out, A0);
  and and_3 (Y2, A1, not_2_out);
  and and_4 (Y3, A1, A0);

  // Notes on the sheet:
  //   2. 2x4 Decoder
  //   Y0=~A1.~A0, Y1=~A1.A0, Y2=A1.~A0, Y3=A1.A0
endmodule

module _03_3x8_Decoder (
  input  A2,
  input  A1,
  input  A0,
  output Y0,
  output Y1,
  output Y2,
  output Y3,
  output Y4,
  output Y5,
  output Y6,
  output Y7
);

  wire not_1_out, not_2_out, not_3_out;

  not not_1 (not_1_out, A2);
  not not_2 (not_2_out, A1);
  not not_3 (not_3_out, A0);
  and and_1 (Y0, not_1_out, not_2_out, not_3_out);
  and and_2 (Y1, not_1_out, not_2_out, A0);
  and and_3 (Y2, not_1_out, A1, not_3_out);
  and and_4 (Y3, not_1_out, A1, A0);
  and and_5 (Y4, A2, not_2_out, not_3_out);
  and and_6 (Y5, A2, not_2_out, A0);
  and and_7 (Y6, A2, A1, not_3_out);
  and and_8 (Y7, A2, A1, A0);

  // Notes on the sheet:
  //   3. 3x8 Line Decoder
  //   Outputs Y0..Y7 decode 3-bit input (A2, A1, A0)
endmodule

module _04_4x1_Multiplexer (
  input  I0,
  input  I1,
  input  I2,
  input  I3,
  input  S1,
  input  S0,
  output Y
);

  wire and_1_out, and_2_out, and_3_out, and_4_out, not_1_out, not_2_out, or_1_out, or_2_out;

  not not_1 (not_1_out, S1);
  not not_2 (not_2_out, S0);
  and and_1 (and_1_out, not_1_out, not_2_out, I0);
  and and_2 (and_2_out, not_1_out, S0, I1);
  and and_3 (and_3_out, S1, not_2_out, I2);
  and and_4 (and_4_out, S1, S0, I3);
  or or_1 (or_1_out, and_1_out, and_2_out);
  or or_2 (or_2_out, and_3_out, and_4_out);
  or or_3 (Y, or_1_out, or_2_out);

  // Notes on the sheet:
  //   4. 4x1 Multiplexer
  //   Y = ~S1.~S0.I0 + ~S1.S0.I1 + S1.~S0.I2 + S1.S0.I3
endmodule

module _05_8x1_Multiplexer (
  input  I0,
  input  I1,
  input  I2,
  input  I3,
  input  I4,
  input  I5,
  input  I6,
  input  I7,
  input  S2,
  input  S1,
  input  S0,
  output Y
);

  wire and_1_out, and_2_out, and_3_out, and_4_out, and_5_out, and_6_out, and_7_out, and_8_out, and_9_out,
       and_10_out, and_11_out, and_12_out, and_13_out, and_14_out, and_15_out, and_16_out, not_1_out,
       not_2_out, not_3_out, or_1_out, or_2_out, or_3_out;

  not not_1 (not_1_out, S2);
  not not_2 (not_2_out, S1);
  not not_3 (not_3_out, S0);
  and and_1 (and_1_out, not_1_out, not_2_out, not_3_out);
  and and_2 (and_2_out, not_1_out, not_2_out, S0);
  and and_3 (and_3_out, not_1_out, S1, not_3_out);
  and and_4 (and_4_out, not_1_out, S1, S0);
  and and_5 (and_5_out, S2, not_2_out, not_3_out);
  and and_6 (and_6_out, S2, not_2_out, S0);
  and and_7 (and_7_out, S2, S1, not_3_out);
  and and_8 (and_8_out, S2, S1, S0);
  and and_9 (and_9_out, and_1_out, I0);
  and and_10 (and_10_out, and_2_out, I1);
  and and_11 (and_11_out, and_3_out, I2);
  and and_12 (and_12_out, and_4_out, I3);
  and and_13 (and_13_out, and_5_out, I4);
  and and_14 (and_14_out, and_6_out, I5);
  and and_15 (and_15_out, and_7_out, I6);
  and and_16 (and_16_out, and_8_out, I7);
  or or_1 (or_1_out, and_9_out, and_10_out, and_11_out);
  or or_2 (or_2_out, and_12_out, and_13_out, and_14_out);
  or or_3 (or_3_out, and_15_out, and_16_out);
  or or_4 (Y, or_1_out, or_2_out, or_3_out);

  // Notes on the sheet:
  //   5. 8x1 Multiplexer
  //   Y = sum(m_i * I_i) selected by (S2, S1, S0)
endmodule

module _06_Octal_to_Binary_Encoder (
  input  D0,
  input  D1,
  input  D2,
  input  D3,
  input  D4,
  input  D5,
  input  D6,
  input  D7,
  output Y2,
  output Y1,
  output Y0
);

  wire or_1_out, or_2_out, or_3_out, or_4_out, or_5_out;

  or or_1 (or_1_out, D4, D5);
  or or_2 (or_2_out, D6, D7);
  or or_3 (or_3_out, D2, D3);
  or or_4 (or_4_out, D1, D3);
  or or_5 (or_5_out, D5, D7);
  or or_6 (Y2, or_1_out, or_2_out);
  or or_7 (Y1, or_3_out, or_2_out);
  or or_8 (Y0, or_4_out, or_5_out);

  // Notes on the sheet:
  //   6. Octal to Binary Encoder (8-to-3)
  //   Y2=D4+D5+D6+D7, Y1=D2+D3+D6+D7, Y0=D1+D3+D5+D7
endmodule

module _07_Decimal_to_BCD_Encoder (
  input  D0,
  input  D1,
  input  D2,
  input  D3,
  input  D4,
  input  D5,
  input  D6,
  input  D7,
  input  D8,
  input  D9,
  output Y3,
  output Y2,
  output Y1,
  output Y0
);

  wire or_1_out, or_2_out, or_3_out, or_4_out, or_5_out;

  or or_1 (or_1_out, D4, D5);
  or or_2 (or_2_out, D6, D7);
  or or_3 (or_3_out, D2, D3);
  or or_4 (or_4_out, D1, D3, D5);
  or or_5 (or_5_out, D7, D9);
  or or_6 (Y3, D8, D9);
  or or_7 (Y2, or_1_out, or_2_out);
  or or_8 (Y1, or_3_out, or_2_out);
  or or_9 (Y0, or_4_out, or_5_out);

  // Notes on the sheet:
  //   7. Decimal to BCD Encoder (10-to-4)
  //   Y3=D8+D9, Y2=D4+D5+D6+D7, Y1=D2+D3+D6+D7, Y0=D1+D3+D5+D7+D9
endmodule

module _08_2x1_Multiplexer (
  input  I0,
  input  I1,
  input  S0,
  output Y
);

  wire and_1_out, and_2_out, not_1_out;

  not not_1 (not_1_out, S0);
  and and_1 (and_1_out, not_1_out, I0);
  and and_2 (and_2_out, S0, I1);
  or or_1 (Y, and_1_out, and_2_out);

  // Notes on the sheet:
  //   8. 2x1 Multiplexer
  //   Y = (~S0 . I0) + (S0 . I1)
endmodule

module _09_3Bit_Even_Parity_NAND (
  input  A,
  input  B,
  input  C,
  output P
);

  wire nand_1_out, nand_2_out, nand_3_out, nand_4_out, nand_5_out, nand_6_out, nand_7_out;

  nand nand_1 (nand_1_out, A, B);
  nand nand_2 (nand_2_out, A, nand_1_out);
  nand nand_3 (nand_3_out, B, nand_1_out);
  nand nand_4 (nand_4_out, nand_2_out, nand_3_out);
  nand nand_5 (nand_5_out, nand_4_out, C);
  nand nand_6 (nand_6_out, nand_4_out, nand_5_out);
  nand nand_7 (nand_7_out, C, nand_5_out);
  nand nand_8 (P, nand_6_out, nand_7_out);

  // Notes on the sheet:
  //   9. 3-Bit Even Parity Generator using NAND Gates
  //   P = A (+) B (+) C implemented using two 4-NAND XOR stages
endmodule

module _10_4Bit_Even_Parity_NAND (
  input  A,
  input  B,
  input  C,
  input  D,
  output P
);

  wire nand_1_out, nand_2_out, nand_3_out, nand_4_out, nand_5_out, nand_6_out, nand_7_out, nand_8_out,
       nand_9_out, nand_10_out, nand_11_out;

  nand nand_1 (nand_1_out, A, B);
  nand nand_2 (nand_2_out, C, D);
  nand nand_3 (nand_3_out, A, nand_1_out);
  nand nand_4 (nand_4_out, B, nand_1_out);
  nand nand_5 (nand_5_out, C, nand_2_out);
  nand nand_6 (nand_6_out, D, nand_2_out);
  nand nand_7 (nand_7_out, nand_3_out, nand_4_out);
  nand nand_8 (nand_8_out, nand_5_out, nand_6_out);
  nand nand_9 (nand_9_out, nand_7_out, nand_8_out);
  nand nand_10 (nand_10_out, nand_7_out, nand_9_out);
  nand nand_11 (nand_11_out, nand_8_out, nand_9_out);
  nand nand_12 (P, nand_10_out, nand_11_out);

  // Notes on the sheet:
  //   10. 4-Bit Even Parity Generator using NAND Gates
  //   P = (A (+) B) (+) (C (+) D) implemented using 12 NAND gates
endmodule

module _11_AND_using_NAND (
  input  A,
  input  B,
  output Y
);

  wire nand_1_out;

  nand nand_1 (nand_1_out, A, B);
  nand nand_2 (Y, nand_1_out, nand_1_out);

  // Notes on the sheet:
  //   11. AND Gate using NAND Gates
  //   Y = A . B = ((A NAND B) NAND (A NAND B))
endmodule

module _12_AND_using_NOR (
  input  A,
  input  B,
  output Y
);

  wire nor_1_out, nor_2_out;

  nor nor_1 (nor_1_out, A, A);
  nor nor_2 (nor_2_out, B, B);
  nor nor_3 (Y, nor_1_out, nor_2_out);

  // Notes on the sheet:
  //   12. AND Gate using NOR Gates
  //   Y = A . B = (A NOR A) NOR (B NOR B)
endmodule

module _13_D_Flip_Flop_NAND (
  input  D,
  input  CLK,
  output Q,
  output Q_bar
);

  wire nand_1_out, nand_2_out, nand_3_out;

  nand nand_1 (nand_1_out, D, D);
  nand nand_2 (nand_2_out, D, CLK);
  nand nand_3 (nand_3_out, CLK, nand_1_out);
  nand nand_4 (Q, nand_2_out, Q_bar);
  nand nand_5 (Q_bar, Q, nand_3_out);

  // Notes on the sheet:
  //   13. D Flip-Flop using NAND Gates
  //   Gated D Flip-Flop constructed with 5 NAND gates
endmodule

module _14_BCD_to_Excess3 (
  input  B3,
  input  B2,
  input  B1,
  input  B0,
  output E3,
  output E2,
  output E1,
  output E0
);

  wire and_1_out, and_2_out, and_3_out, and_4_out, and_5_out, and_6_out, and_7_out, not_1_out, not_2_out;

  not not_1 (not_1_out, B2);
  not not_2 (not_2_out, B1);
  not not_3 (E0, B0);
  and and_1 (and_1_out, B2, B0);
  and and_2 (and_2_out, B2, B1);
  and and_3 (and_3_out, not_1_out, B1);
  and and_4 (and_4_out, not_1_out, B0);
  and and_5 (and_5_out, B2, not_2_out, E0);
  and and_6 (and_6_out, B1, B0);
  and and_7 (and_7_out, not_2_out, E0);
  or or_1 (E3, B3, and_1_out, and_2_out);
  or or_2 (E2, and_3_out, and_4_out, and_5_out);
  or or_3 (E1, and_6_out, and_7_out);

  // Notes on the sheet:
  //   14. BCD to Excess-3 Code Converter
  //   E3=B3+B2.B0+B2.B1, E2=~B2.B1+~B2.B0+B2.~B1.~B0, E1=B1.B0+~B1.~B0, E0=~B0
endmodule

module _15_Full_Adder (
  input  A,
  input  B,
  input  Cin,
  output Sum,
  output Cout
);

  wire and_1_out, and_2_out, xor_1_out;

  xor xor_1 (xor_1_out, A, B);
  and and_1 (and_1_out, A, B);
  xor xor_2 (Sum, xor_1_out, Cin);
  and and_2 (and_2_out, xor_1_out, Cin);
  or or_1 (Cout, and_1_out, and_2_out);

  // Notes on the sheet:
  //   15. Full Adder
  //   Sum = A (+) B (+) Cin, Cout = (A . B) + (Cin . (A (+) B))
endmodule

module _16_Full_Subtractor (
  input  A,
  input  B,
  input  Bin,
  output Diff,
  output Bout
);

  wire and_1_out, and_2_out, not_1_out, not_2_out, xor_1_out;

  xor xor_1 (xor_1_out, A, B);
  not not_1 (not_1_out, A);
  xor xor_2 (Diff, xor_1_out, Bin);
  not not_2 (not_2_out, xor_1_out);
  and and_1 (and_1_out, not_1_out, B);
  and and_2 (and_2_out, not_2_out, Bin);
  or or_1 (Bout, and_1_out, and_2_out);

  // Notes on the sheet:
  //   16. Full Subtractor
  //   Diff = A (+) B (+) Bin, Bout = (~A . B) + (~(A (+) B) . Bin)
endmodule

module _17_Half_Adder (
  input  A,
  input  B,
  output Sum,
  output Carry
);

  xor xor_1 (Sum, A, B);
  and and_1 (Carry, A, B);

  // Notes on the sheet:
  //   17. Half Adder
  //   Sum = A (+) B, Carry = A . B
endmodule

module _18_Half_Subtractor (
  input  A,
  input  B,
  output Diff,
  output Borrow
);

  wire not_1_out;

  not not_1 (not_1_out, A);
  xor xor_1 (Diff, A, B);
  and and_1 (Borrow, not_1_out, B);

  // Notes on the sheet:
  //   18. Half Subtractor
  //   Diff = A (+) B, Borrow = ~A . B
endmodule

module _19_3Var_Boolean_Basic_Gates (
  input  A,
  input  B,
  input  C,
  output Y
);

  wire and_1_out, and_2_out, and_3_out, not_1_out, not_2_out;

  not not_1 (not_1_out, A);
  not not_2 (not_2_out, C);
  and and_1 (and_1_out, A, B);
  and and_2 (and_2_out, not_1_out, C);
  and and_3 (and_3_out, B, not_2_out);
  or or_1 (Y, and_1_out, and_2_out, and_3_out);

  // Notes on the sheet:
  //   19. 3-Variable Boolean Expression using Basic Gates
  //   Y = (A . B) + (~A . C) + (B . ~C)
endmodule

module _20_3Var_Boolean_NAND_Gates (
  input  A,
  input  B,
  input  C,
  output Y
);

  wire nand_1_out, nand_2_out, nand_3_out, nand_4_out, nand_5_out;

  nand nand_1 (nand_1_out, A, A);
  nand nand_2 (nand_2_out, C, C);
  nand nand_3 (nand_3_out, A, B);
  nand nand_4 (nand_4_out, nand_1_out, C);
  nand nand_5 (nand_5_out, B, nand_2_out);
  nand nand_6 (Y, nand_3_out, nand_4_out, nand_5_out);

  // Notes on the sheet:
  //   20. 3-Variable Boolean Expression using NAND Gates
  //   Y = (A . B) + (~A . C) + (B . ~C) implemented strictly with NAND gates
endmodule

module _21_JK_Flip_Flop_NAND (
  input  J,
  input  CLK,
  input  K,
  input  CLR_bar,
  output Q,
  output Q_bar
);

  wire nand_1_out, nand_2_out, nand_3_out, nand_4_out, nand_5_out, nand_6_out, nand_7_out;

  nand nand_1 (nand_1_out, Q_bar, J, CLK);
  nand nand_2 (nand_2_out, CLK, K, Q);
  nand nand_3 (nand_3_out, nand_1_out, nand_4_out);
  nand nand_4 (nand_4_out, nand_3_out, CLR_bar, nand_2_out);
  nand nand_5 (nand_5_out, CLK, CLK);
  nand nand_6 (nand_6_out, nand_3_out, nand_5_out);
  nand nand_7 (nand_7_out, nand_5_out, nand_4_out);
  nand nand_8 (Q, nand_6_out, Q_bar);
  nand nand_9 (Q_bar, nand_7_out, CLR_bar, Q);

  // Notes on the sheet:
  //   21. JK Flip-Flop using NAND Gates
  //   Clocked JK Flip-Flop with 3-input steering NAND gates and cross-coupled latch
endmodule

module _22_Hex_to_Binary_Encoder (
  input  H0,
  input  H1,
  input  H2,
  input  H3,
  input  H4,
  input  H5,
  input  H6,
  input  H7,
  input  H8,
  input  H9,
  input  H10,
  input  H11,
  input  H12,
  input  H13,
  input  H14,
  input  H15,
  output Y3,
  output Y2,
  output Y1,
  output Y0
);

  wire or_1_out, or_2_out, or_3_out, or_4_out, or_5_out, or_6_out, or_7_out, or_8_out, or_9_out, or_10_out,
       or_11_out, or_12_out;

  or or_1 (or_1_out, H8, H9, H10);
  or or_2 (or_2_out, H11, H12, H13);
  or or_3 (or_3_out, H14, H15);
  or or_4 (or_4_out, H4, H5, H6);
  or or_5 (or_5_out, H7, H12, H13);
  or or_6 (or_6_out, H14, H15);
  or or_7 (or_7_out, H2, H3, H6);
  or or_8 (or_8_out, H7, H10, H11);
  or or_9 (or_9_out, H14, H15);
  or or_10 (or_10_out, H1, H3, H5);
  or or_11 (or_11_out, H7, H9, H11);
  or or_12 (or_12_out, H13, H15);
  or or_13 (Y3, or_1_out, or_2_out, or_3_out);
  or or_14 (Y2, or_4_out, or_5_out, or_6_out);
  or or_15 (Y1, or_7_out, or_8_out, or_9_out);
  or or_16 (Y0, or_10_out, or_11_out, or_12_out);

  // Notes on the sheet:
  //   22. Hexadecimal to Binary Encoder (16-to-4)
  //   Encodes H0..H15 into 4-bit binary (Y3, Y2, Y1, Y0)
endmodule

module _23_NAND_using_NOR (
  input  A,
  input  B,
  output Y
);

  wire nor_1_out, nor_2_out, nor_3_out;

  nor nor_1 (nor_1_out, A, A);
  nor nor_2 (nor_2_out, B, B);
  nor nor_3 (nor_3_out, nor_1_out, nor_2_out);
  nor nor_4 (Y, nor_3_out, nor_3_out);

  // Notes on the sheet:
  //   23. NAND Gate using NOR Gates
  //   Y = ~(A . B) implemented using 4 NOR gates
endmodule

module _24_NOR_using_NAND (
  input  A,
  input  B,
  output Y
);

  wire nand_1_out, nand_2_out, nand_3_out;

  nand nand_1 (nand_1_out, A, A);
  nand nand_2 (nand_2_out, B, B);
  nand nand_3 (nand_3_out, nand_1_out, nand_2_out);
  nand nand_4 (Y, nand_3_out, nand_3_out);

  // Notes on the sheet:
  //   24. NOR Gate using NAND Gates
  //   Y = ~(A + B) implemented using 4 NAND gates
endmodule

module _25_OR_using_NAND (
  input  A,
  input  B,
  output Y
);

  wire nand_1_out, nand_2_out;

  nand nand_1 (nand_1_out, A, A);
  nand nand_2 (nand_2_out, B, B);
  nand nand_3 (Y, nand_1_out, nand_2_out);

  // Notes on the sheet:
  //   25. OR Gate using NAND Gates
  //   Y = A + B = (A NAND A) NAND (B NAND B)
endmodule

module _26_OR_using_NOR (
  input  A,
  input  B,
  output Y
);

  wire nor_1_out;

  nor nor_1 (nor_1_out, A, B);
  nor nor_2 (Y, nor_1_out, nor_1_out);

  // Notes on the sheet:
  //   26. OR Gate using NOR Gates
  //   Y = A + B = (A NOR B) NOR (A NOR B)
endmodule

module _27_SR_Flip_Flop_NAND (
  input  S,
  input  CLK,
  input  R,
  output Q,
  output Q_bar
);

  wire nand_1_out, nand_2_out;

  nand nand_1 (nand_1_out, S, CLK);
  nand nand_2 (nand_2_out, CLK, R);
  nand nand_3 (Q, nand_1_out, Q_bar);
  nand nand_4 (Q_bar, Q, nand_2_out);

  // Notes on the sheet:
  //   27. SR Flip-Flop using NAND Gates
  //   Clocked SR Flip-Flop constructed with 4 NAND gates
endmodule

module _28_SR_Flip_Flop_NOR (
  input  R,
  input  CLK,
  input  S,
  output Q,
  output Q_bar
);

  wire nor_1_out, nor_2_out, nor_3_out, nor_4_out, nor_5_out;

  nor nor_1 (nor_1_out, R, R);
  nor nor_2 (nor_2_out, CLK, CLK);
  nor nor_3 (nor_3_out, S, S);
  nor nor_4 (nor_4_out, nor_1_out, nor_2_out);
  nor nor_5 (nor_5_out, nor_2_out, nor_3_out);
  nor nor_6 (Q, nor_4_out, Q_bar);
  nor nor_7 (Q_bar, Q, nor_5_out);

  // Notes on the sheet:
  //   28. SR Flip-Flop using NOR Gates
  //   Clocked SR Flip-Flop constructed exclusively with NOR gates
endmodule

module _29_SR_Latch_NAND (
  input  S_bar,
  input  R_bar,
  output Q,
  output Q_bar
);

  nand nand_1 (Q, S_bar, Q_bar);
  nand nand_2 (Q_bar, Q, R_bar);

  // Notes on the sheet:
  //   29. SR Latch using NAND Gates
  //   Active-Low Cross-Coupled NAND SR Latch (Q = ~(S_bar . Q_bar), Q_bar = ~(R_bar . Q))
endmodule

module _30_SR_Latch_NOR (
  input  R,
  input  S,
  output Q,
  output Q_bar
);

  nor nor_1 (Q, R, Q_bar);
  nor nor_2 (Q_bar, Q, S);

  // Notes on the sheet:
  //   30. SR Latch using NOR Gates
  //   Active-High Cross-Coupled NOR SR Latch (Q = ~(R + Q_bar), Q_bar = ~(S + Q))
endmodule

module _31_Seven_Segment_3Bit (
  input  A2,
  input  A1,
  input  A0,
  output a,
  output b,
  output c,
  output d,
  output e,
  output f,
  output g
);

  wire and_1_out, and_2_out, and_3_out, and_4_out, and_5_out, and_6_out, and_7_out, and_8_out, and_9_out,
       not_1_out, not_2_out, not_3_out, or_4_out;

  not not_1 (not_1_out, A2);
  not not_2 (not_2_out, A1);
  not not_3 (not_3_out, A0);
  and and_1 (and_1_out, A2, A0);
  and and_2 (and_2_out, not_1_out, not_3_out);
  and and_3 (and_3_out, not_2_out, not_3_out);
  and and_4 (and_4_out, A1, A0);
  and and_5 (and_5_out, not_1_out, A1);
  and and_6 (and_6_out, A1, not_3_out);
  and and_7 (and_7_out, A2, not_2_out, A0);
  and and_8 (and_8_out, A2, not_2_out);
  and and_9 (and_9_out, A2, not_3_out);
  or or_1 (a, A1, and_1_out, and_2_out);
  or or_2 (b, not_1_out, and_3_out, and_4_out);
  or or_3 (c, A2, not_2_out, A0);
  or or_4 (or_4_out, and_2_out, and_5_out, and_6_out);
  or or_5 (e, and_2_out, and_6_out);
  or or_6 (f, and_3_out, and_8_out, and_9_out);
  or or_7 (g, and_5_out, and_8_out, and_9_out);
  or or_8 (d, or_4_out, and_7_out);

  // Notes on the sheet:
  //   31. 3-Bit Octal to 7-Segment Display Decoder
  //   Decodes 3-bit input (A2, A1, A0) for digits 0..7 into segments a..g
endmodule

module _32_XNOR_using_NAND (
  input  A,
  input  B,
  output Y
);

  wire nand_1_out, nand_2_out, nand_3_out, nand_4_out;

  nand nand_1 (nand_1_out, A, B);
  nand nand_2 (nand_2_out, A, nand_1_out);
  nand nand_3 (nand_3_out, B, nand_1_out);
  nand nand_4 (nand_4_out, nand_2_out, nand_3_out);
  nand nand_5 (Y, nand_4_out, nand_4_out);

  // Notes on the sheet:
  //   32. XNOR Gate using NAND Gates
  //   Y = ~(A (+) B) implemented using 5 NAND gates
endmodule

module _33_XNOR_using_NOR (
  input  A,
  input  B,
  output Y
);

  wire nor_1_out, nor_2_out, nor_3_out;

  nor nor_1 (nor_1_out, A, B);
  nor nor_2 (nor_2_out, A, nor_1_out);
  nor nor_3 (nor_3_out, B, nor_1_out);
  nor nor_4 (Y, nor_2_out, nor_3_out);

  // Notes on the sheet:
  //   33. XNOR Gate using NOR Gates
  //   Y = ~(A (+) B) implemented using 4 NOR gates
endmodule

module _34_XOR_using_NAND (
  input  A,
  input  B,
  output Y
);

  wire nand_1_out, nand_2_out, nand_3_out;

  nand nand_1 (nand_1_out, A, B);
  nand nand_2 (nand_2_out, A, nand_1_out);
  nand nand_3 (nand_3_out, B, nand_1_out);
  nand nand_4 (Y, nand_2_out, nand_3_out);

  // Notes on the sheet:
  //   34. XOR Gate using NAND Gates
  //   Y = A (+) B implemented using 4 NAND gates
endmodule

module _35_XOR_using_NOR (
  input  A,
  input  B,
  output Y
);

  wire nor_1_out, nor_2_out, nor_3_out, nor_4_out;

  nor nor_1 (nor_1_out, A, B);
  nor nor_2 (nor_2_out, A, nor_1_out);
  nor nor_3 (nor_3_out, B, nor_1_out);
  nor nor_4 (nor_4_out, nor_2_out, nor_3_out);
  nor nor_5 (Y, nor_4_out, nor_4_out);

  // Notes on the sheet:
  //   35. XOR Gate using NOR Gates
  //   Y = A (+) B implemented using 5 NOR gates
endmodule

module _36_AND_Gate (
  input  A,
  input  B,
  output Y
);

  and and_1 (Y, A, B);

  // Notes on the sheet:
  //   36. Basic AND Gate
  //   Y = A . B
endmodule

module _37_OR_Gate (
  input  A,
  input  B,
  output Y
);

  or or_1 (Y, A, B);

  // Notes on the sheet:
  //   37. Basic OR Gate
  //   Y = A + B
endmodule

module _38_NOT_Gate (
  input  A,
  output Y
);

  not not_1 (Y, A);

  // Notes on the sheet:
  //   38. Basic NOT Gate (Inverter)
  //   Y = ~A
endmodule

module _39_XOR_Gate (
  input  A,
  input  B,
  output Y
);

  xor xor_1 (Y, A, B);

  // Notes on the sheet:
  //   39. Basic XOR Gate
  //   Y = A (+) B
endmodule

module _40_XNOR_Gate (
  input  A,
  input  B,
  output Y
);

  xnor xnor_1 (Y, A, B);

  // Notes on the sheet:
  //   40. Basic XNOR Gate
  //   Y = ~(A (+) B)
endmodule

module _41_NOR_Gate (
  input  A,
  input  B,
  output Y
);

  nor nor_1 (Y, A, B);

  // Notes on the sheet:
  //   41. Basic NOR Gate
  //   Y = ~(A + B)
endmodule

module _42_NAND_Gate (
  input  A,
  input  B,
  output Y
);

  nand nand_1 (Y, A, B);

  // Notes on the sheet:
  //   42. Basic NAND Gate
  //   Y = ~(A . B)
endmodule

module _43_T_Flip_Flop (
  input  T,
  input  CLK,
  input  CLR_bar,
  output Q,
  output Q_bar
);

  wire nand_1_out, nand_2_out, nand_3_out, nand_4_out, nand_5_out, nand_6_out, nand_7_out;

  nand nand_1 (nand_1_out, Q_bar, T, CLK);
  nand nand_2 (nand_2_out, CLK, T, Q);
  nand nand_3 (nand_3_out, nand_1_out, nand_4_out);
  nand nand_4 (nand_4_out, nand_3_out, CLR_bar, nand_2_out);
  nand nand_5 (nand_5_out, CLK, CLK);
  nand nand_6 (nand_6_out, nand_3_out, nand_5_out);
  nand nand_7 (nand_7_out, nand_5_out, nand_4_out);
  nand nand_8 (Q, nand_6_out, Q_bar);
  nand nand_9 (Q_bar, nand_7_out, CLR_bar, Q);

  // Notes on the sheet:
  //   43. T (Toggle) Flip-Flop using NAND Gates
  //   Clocked T Flip-Flop with 3-input steering NAND gates and cross-coupled latch
endmodule

module _44_3Var_Boolean_NOR_Gates (
  input  A,
  input  B,
  input  C,
  output Y
);

  wire nor_1_out, nor_2_out, nor_3_out, nor_4_out, nor_5_out;

  nor nor_1 (nor_1_out, A, A);
  nor nor_2 (nor_2_out, C, C);
  nor nor_3 (nor_3_out, A, B);
  nor nor_4 (nor_4_out, nor_1_out, C);
  nor nor_5 (nor_5_out, B, nor_2_out);
  nor nor_6 (Y, nor_3_out, nor_4_out, nor_5_out);

  // Notes on the sheet:
  //   44. 3-Variable Boolean Expression using NOR Gates
  //   Y = (A + B) . (~A + C) . (B + ~C) implemented strictly with NOR gates
endmodule

module _45_4Var_Boolean_Basic_Gates (
  input  A,
  input  B,
  input  C,
  input  D,
  output Y
);

  wire and_1_out, and_2_out, and_3_out, not_1_out, not_2_out;

  not not_1 (not_1_out, A);
  not not_2 (not_2_out, C);
  and and_1 (and_1_out, A, B);
  and and_2 (and_2_out, C, D);
  and and_3 (and_3_out, not_1_out, not_2_out);
  or or_1 (Y, and_1_out, and_2_out, and_3_out);

  // Notes on the sheet:
  //   45. 4-Variable Boolean Expression using Basic Gates
  //   Y = (A . B) + (C . D) + (~A . ~C)
endmodule

module _46_4Var_Boolean_NAND_Gates (
  input  A,
  input  B,
  input  C,
  input  D,
  output Y
);

  wire nand_1_out, nand_2_out, nand_3_out, nand_4_out, nand_5_out;

  nand nand_1 (nand_1_out, A, A);
  nand nand_2 (nand_2_out, C, C);
  nand nand_3 (nand_3_out, A, B);
  nand nand_4 (nand_4_out, C, D);
  nand nand_5 (nand_5_out, nand_1_out, nand_2_out);
  nand nand_6 (Y, nand_3_out, nand_4_out, nand_5_out);

  // Notes on the sheet:
  //   46. 4-Variable Boolean Expression using NAND Gates
  //   Y = (A . B) + (C . D) + (~A . ~C) implemented strictly with NAND gates
endmodule

module _47_NOT_using_NAND (
  input  A,
  output Y
);

  nand nand_1 (Y, A, A);

  // Notes on the sheet:
  //   47. NOT Gate using NAND Gate
  //   Y = ~A = A NAND A
endmodule

module _48_NOT_using_NOR (
  input  A,
  output Y
);

  nor nor_1 (Y, A, A);

  // Notes on the sheet:
  //   48. NOT Gate using NOR Gate
  //   Y = ~A = A NOR A
endmodule

module _49_2Var_Boolean_Basic_Gates (
  input  A,
  input  B,
  output Y
);

  wire and_1_out, and_2_out, not_1_out, not_2_out;

  not not_1 (not_1_out, A);
  not not_2 (not_2_out, B);
  and and_1 (and_1_out, A, not_2_out);
  and and_2 (and_2_out, not_1_out, B);
  or or_1 (Y, and_1_out, and_2_out);

  // Notes on the sheet:
  //   49. 2-Variable Boolean Expression using Basic Gates
  //   Y = (A . ~B) + (~A . B)
endmodule

module _50_2Var_Boolean_NAND_Gates (
  input  A,
  input  B,
  output Y
);

  wire nand_1_out, nand_2_out, nand_3_out, nand_4_out;

  nand nand_1 (nand_1_out, A, A);
  nand nand_2 (nand_2_out, B, B);
  nand nand_3 (nand_3_out, A, nand_2_out);
  nand nand_4 (nand_4_out, nand_1_out, B);
  nand nand_5 (Y, nand_3_out, nand_4_out);

  // Notes on the sheet:
  //   50. 2-Variable Boolean Expression using NAND Gates
  //   Y = (A . ~B) + (~A . B) implemented strictly with NAND gates
endmodule
