// Logisim project DEE_50_Lab_Circuits.circ as structural Verilog: 50 circuits, main circuit 01_1_to_4_demultiplexer
// 1-to-4 demultiplexer
module _01_1_to_4_demultiplexer (
  input  D,
  input  S1,
  input  S0
);

  wire and_1_out, and_2_out, and_3_out, and_4_out, and_5_out, and_6_out, and_7_out, and_8_out, not_1_out,
       not_2_out, not_3_out, not_4_out;

  not not_1 (not_1_out, S1);
  not not_2 (not_2_out, S0);
  not not_3 (not_3_out, S1);
  not not_4 (not_4_out, S0);
  and and_1 (and_1_out, S1, S0);
  and and_2 (and_2_out, not_1_out, not_2_out);
  and and_3 (and_3_out, not_3_out, S0);
  and and_4 (and_4_out, S1, not_4_out);
  and and_5 (and_5_out, D, and_1_out);
  and and_6 (and_6_out, D, and_2_out);
  and and_7 (and_7_out, D, and_3_out);
  and and_8 (and_8_out, D, and_4_out);
  LED led_1 (.in(and_6_out));
  LED led_2 (.in(and_7_out));
  LED led_3 (.in(and_8_out));
  LED led_4 (.in(and_5_out));

  // Notes on the sheet:
  //   1-to-4 demultiplexer
  //   One data input; S1 is the most-significant select bit.
  //   Y0
  //   Y1
  //   Y2
  //   Y3
endmodule

// 2-to-4 decoder
module _02_2_to_4_decoder (
  input  A,
  input  B
);

  wire and_1_out, and_2_out, and_3_out, and_4_out, not_1_out, not_2_out, not_3_out, not_4_out;

  not not_1 (not_1_out, A);
  not not_2 (not_2_out, B);
  not not_3 (not_3_out, A);
  not not_4 (not_4_out, B);
  and and_1 (and_1_out, A, B);
  and and_2 (and_2_out, not_1_out, not_2_out);
  and and_3 (and_3_out, not_3_out, B);
  and and_4 (and_4_out, A, not_4_out);
  LED led_1 (.in(and_2_out));
  LED led_2 (.in(and_3_out));
  LED led_3 (.in(and_4_out));
  LED led_4 (.in(and_1_out));

  // Notes on the sheet:
  //   2-to-4 decoder
  //   Active-high outputs; A is the most-significant input bit.
  //   Y0
  //   Y1
  //   Y2
  //   Y3
endmodule

// 3-to-8 decoder
module _03_3_to_8_decoder (
  input  A,
  input  B,
  input  C
);

  wire and_1_out, and_2_out, and_3_out, and_4_out, and_5_out, and_6_out, and_7_out, and_8_out, and_9_out,
       and_10_out, and_11_out, and_12_out, and_13_out, and_14_out, and_15_out, and_16_out, not_1_out,
       not_2_out, not_3_out, not_4_out, not_5_out, not_6_out, not_7_out, not_8_out, not_9_out, not_10_out,
       not_11_out, not_12_out;

  not not_1 (not_1_out, A);
  not not_2 (not_2_out, B);
  not not_3 (not_3_out, C);
  not not_4 (not_4_out, A);
  not not_5 (not_5_out, B);
  not not_6 (not_6_out, A);
  not not_7 (not_7_out, C);
  not not_8 (not_8_out, A);
  not not_9 (not_9_out, B);
  not not_10 (not_10_out, C);
  not not_11 (not_11_out, B);
  not not_12 (not_12_out, C);
  and and_1 (and_1_out, A, B);
  and and_2 (and_2_out, A, B);
  and and_3 (and_3_out, not_1_out, not_2_out);
  and and_4 (and_4_out, not_4_out, not_5_out);
  and and_5 (and_5_out, not_6_out, B);
  and and_6 (and_6_out, not_8_out, B);
  and and_7 (and_7_out, A, not_9_out);
  and and_8 (and_8_out, A, not_11_out);
  and and_9 (and_9_out, and_1_out, not_12_out);
  and and_10 (and_10_out, and_2_out, C);
  and and_11 (and_11_out, and_3_out, not_3_out);
  and and_12 (and_12_out, and_4_out, C);
  and and_13 (and_13_out, and_5_out, not_7_out);
  and and_14 (and_14_out, and_6_out, C);
  and and_15 (and_15_out, and_7_out, not_10_out);
  and and_16 (and_16_out, and_8_out, C);
  LED led_1 (.in(and_11_out));
  LED led_2 (.in(and_12_out));
  LED led_3 (.in(and_13_out));
  LED led_4 (.in(and_14_out));
  LED led_5 (.in(and_15_out));
  LED led_6 (.in(and_16_out));
  LED led_7 (.in(and_9_out));
  LED led_8 (.in(and_10_out));

  // Notes on the sheet:
  //   3-to-8 decoder
  //   Active-high outputs; A is the most-significant input bit.
  //   Y0
  //   Y1
  //   Y2
  //   Y3
  //   Y4
  //   Y5
  //   Y6
  //   Y7
endmodule

// 4-to-1 multiplexer
module _04_4_to_1_multiplexer (
  input  D0,
  input  D1,
  input  D2,
  input  D3,
  input  S1,
  input  S0
);

  wire and_1_out, and_2_out, and_3_out, and_4_out, and_5_out, and_6_out, and_7_out, and_8_out, not_1_out,
       not_2_out, or_1_out, or_2_out, or_3_out;

  not not_1 (not_1_out, S1);
  not not_2 (not_2_out, S0);
  and and_1 (and_1_out, D2, S1);
  and and_2 (and_2_out, D3, S1);
  and and_3 (and_3_out, D0, not_1_out);
  and and_4 (and_4_out, D1, not_1_out);
  and and_5 (and_5_out, and_1_out, not_2_out);
  and and_6 (and_6_out, and_2_out, S0);
  and and_7 (and_7_out, and_3_out, not_2_out);
  and and_8 (and_8_out, and_4_out, S0);
  or or_1 (or_1_out, and_5_out, and_6_out);
  or or_2 (or_2_out, and_7_out, and_8_out);
  or or_3 (or_3_out, or_2_out, or_1_out);
  LED led_1 (.in(or_3_out));

  // Notes on the sheet:
  //   4-to-1 multiplexer
  //   S1 is the most-significant select bit; D0 is selected by S1S0=00.
  //   Y
endmodule

// 8-to-1 multiplexer
module _05_8_to_1_multiplexer (
  input  D0,
  input  D1,
  input  D2,
  input  D3,
  input  D4,
  input  D5,
  input  D6,
  input  D7,
  input  S2,
  input  S1,
  input  S0
);

  wire and_1_out, and_2_out, and_3_out, and_4_out, and_5_out, and_6_out, and_7_out, and_8_out, and_9_out,
       and_10_out, and_11_out, and_12_out, and_13_out, and_14_out, and_15_out, and_16_out, and_17_out,
       and_18_out, and_19_out, and_20_out, and_21_out, and_22_out, and_23_out, and_24_out, not_1_out,
       not_2_out, not_3_out, or_1_out, or_2_out, or_3_out, or_4_out, or_5_out, or_6_out, or_7_out;

  not not_1 (not_1_out, S2);
  not not_2 (not_2_out, S1);
  not not_3 (not_3_out, S0);
  and and_1 (and_1_out, S1, S0);
  and and_2 (and_2_out, D4, S2);
  and and_3 (and_3_out, D5, S2);
  and and_4 (and_4_out, D6, S2);
  and and_5 (and_5_out, D7, S2);
  and and_6 (and_6_out, S1, S0);
  and and_7 (and_7_out, D0, not_1_out);
  and and_8 (and_8_out, not_2_out, not_3_out);
  and and_9 (and_9_out, D1, not_1_out);
  and and_10 (and_10_out, not_2_out, S0);
  and and_11 (and_11_out, D2, not_1_out);
  and and_12 (and_12_out, S1, not_3_out);
  and and_13 (and_13_out, D3, not_1_out);
  and and_14 (and_14_out, not_2_out, not_3_out);
  and and_15 (and_15_out, not_2_out, S0);
  and and_16 (and_16_out, S1, not_3_out);
  and and_17 (and_17_out, and_5_out, and_6_out);
  and and_18 (and_18_out, and_7_out, and_8_out);
  and and_19 (and_19_out, and_9_out, and_10_out);
  and and_20 (and_20_out, and_11_out, and_12_out);
  and and_21 (and_21_out, and_13_out, and_1_out);
  and and_22 (and_22_out, and_2_out, and_14_out);
  and and_23 (and_23_out, and_3_out, and_15_out);
  and and_24 (and_24_out, and_4_out, and_16_out);
  or or_1 (or_1_out, and_18_out, and_19_out);
  or or_2 (or_2_out, and_20_out, and_21_out);
  or or_3 (or_3_out, and_22_out, and_23_out);
  or or_4 (or_4_out, and_24_out, and_17_out);
  or or_5 (or_5_out, or_1_out, or_2_out);
  or or_6 (or_6_out, or_3_out, or_4_out);
  or or_7 (or_7_out, or_5_out, or_6_out);
  LED led_1 (.in(or_7_out));

  // Notes on the sheet:
  //   8-to-1 multiplexer
  //   S2 is the most-significant select bit; D0 is selected by S2S1S0=000.
  //   Y
endmodule

// Octal-to-binary encoder
module _06_Octal_to_binary_encoder (
  input  D0,
  input  D1,
  input  D2,
  input  D3,
  input  D4,
  input  D5,
  input  D6,
  input  D7
);

  wire or_1_out, or_2_out, or_3_out, or_4_out, or_5_out, or_6_out, or_7_out, or_8_out, or_9_out;

  or or_1 (or_1_out, D4, D5);
  or or_2 (or_2_out, D6, D7);
  or or_3 (or_3_out, D2, D3);
  or or_4 (or_4_out, D6, D7);
  or or_5 (or_5_out, D1, D3);
  or or_6 (or_6_out, D5, D7);
  or or_7 (or_7_out, or_1_out, or_2_out);
  or or_8 (or_8_out, or_3_out, or_4_out);
  or or_9 (or_9_out, or_5_out, or_6_out);
  LED led_1 (.in(or_7_out));
  LED led_2 (.in(or_8_out));
  LED led_3 (.in(or_9_out));

  // Notes on the sheet:
  //   Octal-to-binary encoder
  //   One-hot inputs D0-D7; outputs are B2 B1 B0.
  //   B2
  //   B1
  //   B0
endmodule

// Decimal-to-BCD encoder
module _07_Decimal_to_BCD_encoder (
  input  D0,
  input  D1,
  input  D2,
  input  D3,
  input  D4,
  input  D5,
  input  D6,
  input  D7,
  input  D8,
  input  D9
);

  wire or_1_out, or_2_out, or_3_out, or_4_out, or_5_out, or_6_out, or_7_out, or_8_p3, or_9_out, or_10_out,
       or_11_p3;

  or or_1 (or_1_out, D8, D9);
  or or_2 (or_2_out, D4, D5);
  or or_3 (or_3_out, D6, D7);
  or or_4 (or_4_out, D2, D3);
  or or_5 (or_5_out, D6, D7);
  or or_6 (or_6_out, D1, D3);
  or or_7 (or_7_out, D5, D7);
  // OR_Gate or_8: pin names not known; wires that end beside it: or_2_out, or_3_out, or_8_p3
  or or_9 (or_9_out, or_4_out, or_5_out);
  or or_10 (or_10_out, or_6_out, or_7_out);
  // OR_Gate or_11: pin names not known; wires that end beside it: or_10_out, D9, or_11_p3
  LED led_1 (.in(or_1_out));
  LED led_2 (.in(or_8_p3));
  LED led_3 (.in(or_9_out));
  LED led_4 (.in(or_11_p3));

  // Notes on the sheet:
  //   Decimal-to-BCD encoder
  //   One-hot decimal inputs D0-D9; B3 B2 B1 B0 is the BCD result.
  //   B3
  //   B2
  //   B1
  //   B0
endmodule

// 2-to-1 multiplexer
module _08_2_to_1_multiplexer (
  input  D0,
  input  D1,
  input  S
);

  wire and_1_out, and_2_out, not_1_out, or_1_out;

  not not_1 (not_1_out, S);
  and and_1 (and_1_out, D1, S);
  and and_2 (and_2_out, D0, not_1_out);
  or or_1 (or_1_out, and_2_out, and_1_out);
  LED led_1 (.in(or_1_out));

  // Notes on the sheet:
  //   2-to-1 multiplexer
  //   S=0 selects D0; S=1 selects D1.
  //   Y
endmodule

// 3-bit even parity generator using NAND gates
module _09_3_bit_even_parity_generator_using_NAND_gates (
  input  A,
  input  B,
  input  C
);

  wire nand_1_p3, nand_2_p4, nand_3_p4, nand_4_p3, nand_5_p3, nand_6_p4, nand_7_p4, nand_8_p3;

  // NAND_Gate nand_1: pin names not known; wires that end beside it: A, B, nand_1_p3
  // NAND_Gate nand_2: pin names not known; wires that end beside it: A, nand_1_p3, B, nand_2_p4
  // NAND_Gate nand_3: pin names not known; wires that end beside it: nand_1_p3, B, nand_1_p3, nand_3_p4
  // NAND_Gate nand_4: pin names not known; wires that end beside it: nand_2_p4, nand_3_p4, nand_4_p3
  // NAND_Gate nand_5: pin names not known; wires that end beside it: nand_4_p3, C, nand_5_p3
  // NAND_Gate nand_6: pin names not known; wires that end beside it: nand_4_p3, nand_5_p3, C, nand_6_p4
  // NAND_Gate nand_7: pin names not known; wires that end beside it: nand_5_p3, C, nand_5_p3, nand_7_p4
  // NAND_Gate nand_8: pin names not known; wires that end beside it: nand_6_p4, nand_7_p4, nand_8_p3
  LED led_1 (.in(nand_8_p3));

  // Notes on the sheet:
  //   3-bit even parity generator using NAND gates
  //   P=A XOR B XOR C; P makes the total number of 1s even.
  //   P
endmodule

// 4-bit even parity generator using NAND gates
module _10_4_bit_even_parity_generator_using_NAND_gates (
  input  A,
  input  B,
  input  C,
  input  D
);

  wire nand_1_p3, nand_2_p4, nand_3_p4, nand_4_p3, nand_5_p3, nand_6_p4, nand_7_p4, nand_8_p3, nand_9_p3,
       nand_10_p4, nand_11_p4, nand_12_p3;

  // NAND_Gate nand_1: pin names not known; wires that end beside it: A, B, nand_1_p3
  // NAND_Gate nand_2: pin names not known; wires that end beside it: A, nand_1_p3, B, nand_2_p4
  // NAND_Gate nand_3: pin names not known; wires that end beside it: nand_1_p3, B, nand_1_p3, nand_3_p4
  // NAND_Gate nand_4: pin names not known; wires that end beside it: nand_2_p4, nand_3_p4, nand_4_p3
  // NAND_Gate nand_5: pin names not known; wires that end beside it: nand_4_p3, C, nand_5_p3
  // NAND_Gate nand_6: pin names not known; wires that end beside it: nand_4_p3, nand_5_p3, C, nand_6_p4
  // NAND_Gate nand_7: pin names not known; wires that end beside it: nand_5_p3, C, nand_5_p3, nand_7_p4
  // NAND_Gate nand_8: pin names not known; wires that end beside it: nand_6_p4, nand_7_p4, nand_8_p3
  // NAND_Gate nand_9: pin names not known; wires that end beside it: nand_8_p3, D, nand_9_p3
  // NAND_Gate nand_10: pin names not known; wires that end beside it: nand_8_p3, nand_9_p3, D, nand_10_p4
  // NAND_Gate nand_11: pin names not known; wires that end beside it: nand_9_p3, D, nand_9_p3, nand_11_p4
  // NAND_Gate nand_12: pin names not known; wires that end beside it: nand_10_p4, nand_11_p4, nand_12_p3
  LED led_1 (.in(nand_12_p3));

  // Notes on the sheet:
  //   4-bit even parity generator using NAND gates
  //   P=A XOR B XOR C XOR D; P makes the total number of 1s even.
  //   P
endmodule

// AND gate using NAND gate
module _11_AND_gate_using_NAND_gate (
  input  A,
  input  B
);

  wire nand_1_p3, nand_2_p3;

  // NAND_Gate nand_1: pin names not known; wires that end beside it: A, B, nand_1_p3
  // NAND_Gate nand_2: pin names not known; wires that end beside it: nand_1_p3, nand_1_p3, nand_2_p3
  LED led_1 (.in(nand_2_p3));

  // Notes on the sheet:
  //   AND gate using NAND gate
  //   NAND followed by NAND inversion.
  //   Y
endmodule

// AND gate using NOR gate
module _12_AND_gate_using_NOR_gate (
  input  A,
  input  B
);

  wire nor_1_p4, nor_2_p4, nor_3_p3;

  // NOR_Gate nor_1: pin names not known; wires that end beside it: A, A, B, nor_1_p4
  // NOR_Gate nor_2: pin names not known; wires that end beside it: A, B, B, nor_2_p4
  // NOR_Gate nor_3: pin names not known; wires that end beside it: nor_1_p4, nor_2_p4, nor_3_p3
  LED led_1 (.in(nor_3_p3));

  // Notes on the sheet:
  //   AND gate using NOR gate
  //   Invert each input with NOR, then NOR the inverted inputs.
  //   Y
endmodule

// D flip-flop using NAND gates
module _13_D_flip_flop_using_NAND_gates (
  input  D,
  input  CLK
);

  wire nand_1_p3, nand_2_p3, nand_3_p3, nand_4_p3, nand_5_p2, nand_5_p3, nand_7_p3, nand_8_p3, nand_9_p2,
       nand_9_p3;

  // NAND_Gate nand_1: pin names not known; wires that end beside it: D, D, nand_1_p3
  // NAND_Gate nand_2: pin names not known; wires that end beside it: CLK, CLK, nand_2_p3
  // NAND_Gate nand_3: pin names not known; wires that end beside it: D, CLK, nand_3_p3
  // NAND_Gate nand_4: pin names not known; wires that end beside it: nand_1_p3, CLK, nand_4_p3
  // NAND_Gate nand_5: pin names not known; wires that end beside it: nand_3_p3, nand_5_p2, nand_5_p3
  // NAND_Gate nand_6: pin names not known; wires that end beside it: nand_4_p3, nand_5_p3, nand_5_p2
  // NAND_Gate nand_7: pin names not known; wires that end beside it: nand_5_p3, nand_2_p3, nand_7_p3
  // NAND_Gate nand_8: pin names not known; wires that end beside it: nand_5_p2, nand_2_p3, nand_8_p3
  // NAND_Gate nand_9: pin names not known; wires that end beside it: nand_7_p3, nand_9_p2, nand_9_p3
  // NAND_Gate nand_10: pin names not known; wires that end beside it: nand_8_p3, nand_9_p3, nand_9_p2
  LED led_1 (.in(nand_9_p3));
  LED led_2 (.in(nand_9_p2));

  // Notes on the sheet:
  //   D flip-flop using NAND gates
  //   Master-slave circuit; falling-edge triggered.
  //   Q
  //   Qbar
endmodule

// Excess-3 code conversion from BCD
module _14_Excess_3_code_conversion_from_BCD (
  input  A,
  input  B,
  input  C,
  input  D
);

  wire and_1_p3, not_1_out, or_1_out, xnor_1_out, xor_1_p3, xor_2_p3;

  not not_1 (not_1_out, D);
  xnor xnor_1 (xnor_1_out, C, D);
  or or_1 (or_1_out, C, D);
  // XOR_Gate xor_1: pin names not known; wires that end beside it: B, or_1_out, xor_1_p3
  // AND_Gate and_1: pin names not known; wires that end beside it: B, or_1_out, and_1_p3
  // XOR_Gate xor_2: pin names not known; wires that end beside it: A, and_1_p3, xor_2_p3
  LED led_1 (.in(xor_2_p3));
  LED led_2 (.in(xor_1_p3));
  LED led_3 (.in(xnor_1_out));
  LED led_4 (.in(not_1_out));

  // Notes on the sheet:
  //   Excess-3 code conversion from BCD
  //   For valid BCD A B C D, outputs equal the binary value plus 0011.
  //   E3
  //   E2
  //   E1
  //   E0
endmodule

// Full adder
module _15_Full_adder (
  input  A,
  input  B,
  input  Cin
);

  wire and_1_out, and_2_out, or_1_p3, xor_1_p3, xor_2_p3;

  // XOR_Gate xor_1: pin names not known; wires that end beside it: A, B, xor_1_p3
  and and_1 (and_1_out, A, B);
  // XOR_Gate xor_2: pin names not known; wires that end beside it: xor_1_p3, Cin, xor_2_p3
  and and_2 (and_2_out, xor_1_p3, Cin);
  // OR_Gate or_1: pin names not known; wires that end beside it: and_1_out, and_2_out, or_1_p3
  LED led_1 (.in(xor_2_p3));
  LED led_2 (.in(or_1_p3));

  // Notes on the sheet:
  //   Full adder
  //   S=A XOR B XOR Cin; Cout=AB + Cin(A XOR B).
  //   S
  //   Cout
endmodule

// Full subtractor
module _16_Full_subtractor (
  input  A,
  input  B,
  input  Bin
);

  wire and_1_out, and_2_out, not_1_out, or_1_p3, xnor_1_out, xor_1_p3, xor_2_p3;

  // XOR_Gate xor_1: pin names not known; wires that end beside it: A, B, xor_1_p3
  not not_1 (not_1_out, A);
  xnor xnor_1 (xnor_1_out, A, B);
  // XOR_Gate xor_2: pin names not known; wires that end beside it: xor_1_p3, Bin, xor_2_p3
  and and_1 (and_1_out, not_1_out, B);
  and and_2 (and_2_out, xnor_1_out, Bin);
  // OR_Gate or_1: pin names not known; wires that end beside it: and_1_out, and_2_out, or_1_p3
  LED led_1 (.in(xor_2_p3));
  LED led_2 (.in(or_1_p3));

  // Notes on the sheet:
  //   Full subtractor
  //   Diff=A XOR B XOR Bin; Bout=A'B + (A XNOR B)Bin.
  //   Diff
  //   Bout
endmodule

// Half adder
module _17_Half_adder (
  input  A,
  input  B
);

  wire and_1_out, xor_1_p3;

  // XOR_Gate xor_1: pin names not known; wires that end beside it: A, B, xor_1_p3
  and and_1 (and_1_out, A, B);
  LED led_1 (.in(xor_1_p3));
  LED led_2 (.in(and_1_out));

  // Notes on the sheet:
  //   Half adder
  //   S=A XOR B; Carry=AB.
  //   S
  //   Carry
endmodule

// Half subtractor
module _18_Half_subtractor (
  input  A,
  input  B
);

  wire and_1_p3, not_1_out, xor_1_p3;

  // XOR_Gate xor_1: pin names not known; wires that end beside it: A, B, xor_1_p3
  not not_1 (not_1_out, A);
  // AND_Gate and_1: pin names not known; wires that end beside it: not_1_out, B, and_1_p3
  LED led_1 (.in(xor_1_p3));
  LED led_2 (.in(and_1_p3));

  // Notes on the sheet:
  //   Half subtractor
  //   Diff=A XOR B; Borrow=A'B.
  //   Diff
  //   Borrow
endmodule

// F(A,B,C) = A'B + BC' + AC
module _19_F_A_B_C_A_B_BC_AC (
  input  A,
  input  B,
  input  C
);

  wire and_1_out, and_2_out, and_3_out, not_1_out, not_2_out, or_1_out, or_2_out;

  not not_1 (not_1_out, A);
  not not_2 (not_2_out, C);
  and and_1 (and_1_out, A, C);
  and and_2 (and_2_out, not_1_out, B);
  and and_3 (and_3_out, B, not_2_out);
  or or_1 (or_1_out, and_2_out, and_3_out);
  or or_2 (or_2_out, or_1_out, and_1_out);
  LED led_1 (.in(or_2_out));

  // Notes on the sheet:
  //   F(A,B,C) = A'B + BC' + AC
  //   Representative expression used because the index page does not specify F.
  //   F
endmodule

// F(A,B,C) = A'B + BC' + AC
module _20_F_A_B_C_A_B_BC_AC (
  input  A,
  input  B,
  input  C
);

  wire nand_1_p4, nand_2_p5, nand_3_p4, nand_4_p4, nand_5_p4, nand_6_p3, nand_7_p3, nand_8_p3;

  // NAND_Gate nand_1: pin names not known; wires that end beside it: A, A, C, nand_1_p4
  // NAND_Gate nand_2: pin names not known; wires that end beside it: A, C, C, A, nand_2_p5
  // NAND_Gate nand_3: pin names not known; wires that end beside it: C, A, C, nand_3_p4
  // NAND_Gate nand_4: pin names not known; wires that end beside it: nand_1_p4, B, B, nand_4_p4
  // NAND_Gate nand_5: pin names not known; wires that end beside it: B, B, nand_2_p5, nand_5_p4
  // NAND_Gate nand_6: pin names not known; wires that end beside it: nand_4_p4, nand_5_p4, nand_6_p3
  // NAND_Gate nand_7: pin names not known; wires that end beside it: nand_6_p3, nand_6_p3, nand_7_p3
  // NAND_Gate nand_8: pin names not known; wires that end beside it: nand_7_p3, nand_3_p4, nand_8_p3
  LED led_1 (.in(nand_8_p3));

  // Notes on the sheet:
  //   F(A,B,C) = A'B + BC' + AC
  //   Representative expression used because the index page does not specify F.
  //   F
endmodule

// JK flip-flop using NAND gates
module _21_JK_flip_flop_using_NAND_gates (
  input  J,
  input  K,
  input  CLK
);

  wire nand_1_p3, nand_2_p3, nand_2_p4, nand_3_p3, nand_3_p4, nand_4_p2, nand_4_p3, nand_6_p3, nand_7_p3;

  // NAND_Gate nand_1: pin names not known; wires that end beside it: CLK, CLK, nand_1_p3
  // NAND_Gate nand_2: pin names not known; wires that end beside it: J, CLK, nand_2_p3, nand_2_p4
  // NAND_Gate nand_3: pin names not known; wires that end beside it: K, CLK, nand_3_p3, nand_3_p4
  // NAND_Gate nand_4: pin names not known; wires that end beside it: nand_2_p4, nand_4_p2, nand_4_p3
  // NAND_Gate nand_5: pin names not known; wires that end beside it: nand_3_p4, nand_4_p3, nand_4_p2
  // NAND_Gate nand_6: pin names not known; wires that end beside it: nand_4_p3, nand_1_p3, nand_6_p3
  // NAND_Gate nand_7: pin names not known; wires that end beside it: nand_4_p2, nand_1_p3, nand_7_p3
  // NAND_Gate nand_8: pin names not known; wires that end beside it: nand_6_p3, nand_2_p3, nand_3_p3
  // NAND_Gate nand_9: pin names not known; wires that end beside it: nand_7_p3, nand_3_p3, nand_2_p3
  LED led_1 (.in(nand_3_p3));
  LED led_2 (.in(nand_2_p3));

  // Notes on the sheet:
  //   JK flip-flop using NAND gates
  //   Falling-edge master-slave implementation using NAND gates.
  //   Q
  //   Qbar
endmodule

// Hexadecimal-to-binary encoder
module _22_Hexadecimal_to_binary_encoder (
  input  D0,
  input  D1,
  input  D2,
  input  D3,
  input  D4,
  input  D5,
  input  D6,
  input  D7,
  input  D8,
  input  D9,
  input  DA,
  input  DB,
  input  DC,
  input  DD,
  input  DE,
  input  DF
);

  wire or_1_out, or_2_out, or_3_out, or_4_out, or_5_out, or_6_out, or_7_out, or_8_out, or_9_out, or_10_out,
       or_11_out, or_12_out, or_13_out, or_14_out, or_15_out, or_16_out, or_17_out, or_18_out, or_19_out,
       or_20_out, or_21_out, or_22_out, or_23_out, or_24_out, or_25_out, or_26_out, or_27_out, or_28_out;

  or or_1 (or_1_out, D8, D9);
  or or_2 (or_2_out, DA, DB);
  or or_3 (or_3_out, DC, DD);
  or or_4 (or_4_out, DE, DF);
  or or_5 (or_5_out, D4, D5);
  or or_6 (or_6_out, D6, D7);
  or or_7 (or_7_out, DC, DD);
  or or_8 (or_8_out, DE, DF);
  or or_9 (or_9_out, D2, D3);
  or or_10 (or_10_out, D6, D7);
  or or_11 (or_11_out, DA, DB);
  or or_12 (or_12_out, DE, DF);
  or or_13 (or_13_out, D1, D3);
  or or_14 (or_14_out, D5, D7);
  or or_15 (or_15_out, D9, DB);
  or or_16 (or_16_out, DD, DF);
  or or_17 (or_17_out, or_1_out, or_2_out);
  or or_18 (or_18_out, or_3_out, or_4_out);
  or or_19 (or_19_out, or_5_out, or_6_out);
  or or_20 (or_20_out, or_7_out, or_8_out);
  or or_21 (or_21_out, or_9_out, or_10_out);
  or or_22 (or_22_out, or_11_out, or_12_out);
  or or_23 (or_23_out, or_13_out, or_14_out);
  or or_24 (or_24_out, or_15_out, or_16_out);
  or or_25 (or_25_out, or_17_out, or_18_out);
  or or_26 (or_26_out, or_19_out, or_20_out);
  or or_27 (or_27_out, or_21_out, or_22_out);
  or or_28 (or_28_out, or_23_out, or_24_out);
  LED led_1 (.in(or_25_out));
  LED led_2 (.in(or_26_out));
  LED led_3 (.in(or_27_out));
  LED led_4 (.in(or_28_out));

  // Notes on the sheet:
  //   Hexadecimal-to-binary encoder
  //   One-hot inputs D0-D15; outputs are B3 B2 B1 B0.
  //   B3
  //   B2
  //   B1
  //   B0
endmodule

// NAND gate using NOR gates
module _23_NAND_gate_using_NOR_gates (
  input  A,
  input  B
);

  wire nor_1_p4, nor_2_p4, nor_3_p3, nor_4_p3;

  // NOR_Gate nor_1: pin names not known; wires that end beside it: A, A, B, nor_1_p4
  // NOR_Gate nor_2: pin names not known; wires that end beside it: A, B, B, nor_2_p4
  // NOR_Gate nor_3: pin names not known; wires that end beside it: nor_1_p4, nor_2_p4, nor_3_p3
  // NOR_Gate nor_4: pin names not known; wires that end beside it: nor_3_p3, nor_3_p3, nor_4_p3
  LED led_1 (.in(nor_4_p3));

  // Notes on the sheet:
  //   NAND gate using NOR gates
  //   NOR-only realization of Y=(AB)'.
  //   Y
endmodule

// NOR gate using NAND gates
module _24_NOR_gate_using_NAND_gates (
  input  A,
  input  B
);

  wire nand_1_p4, nand_2_p4, nand_3_p3, nand_4_p3;

  // NAND_Gate nand_1: pin names not known; wires that end beside it: A, A, B, nand_1_p4
  // NAND_Gate nand_2: pin names not known; wires that end beside it: A, B, B, nand_2_p4
  // NAND_Gate nand_3: pin names not known; wires that end beside it: nand_1_p4, nand_2_p4, nand_3_p3
  // NAND_Gate nand_4: pin names not known; wires that end beside it: nand_3_p3, nand_3_p3, nand_4_p3
  LED led_1 (.in(nand_4_p3));

  // Notes on the sheet:
  //   NOR gate using NAND gates
  //   NAND-only realization of Y=(A+B)'.
  //   Y
endmodule

// OR gate using NAND gates
module _25_OR_gate_using_NAND_gates (
  input  A,
  input  B
);

  wire nand_1_p4, nand_2_p4, nand_3_p3;

  // NAND_Gate nand_1: pin names not known; wires that end beside it: A, A, B, nand_1_p4
  // NAND_Gate nand_2: pin names not known; wires that end beside it: A, B, B, nand_2_p4
  // NAND_Gate nand_3: pin names not known; wires that end beside it: nand_1_p4, nand_2_p4, nand_3_p3
  LED led_1 (.in(nand_3_p3));

  // Notes on the sheet:
  //   OR gate using NAND gates
  //   Invert inputs with NAND gates, then NAND them.
  //   Y
endmodule

// OR gate using NOR gates
module _26_OR_gate_using_NOR_gates (
  input  A,
  input  B
);

  wire nor_1_p3, nor_2_p3;

  // NOR_Gate nor_1: pin names not known; wires that end beside it: A, B, nor_1_p3
  // NOR_Gate nor_2: pin names not known; wires that end beside it: nor_1_p3, nor_1_p3, nor_2_p3
  LED led_1 (.in(nor_2_p3));

  // Notes on the sheet:
  //   OR gate using NOR gates
  //   NOR followed by NOR inversion.
  //   Y
endmodule

// Clocked SR latch using NAND gates
module _27_Clocked_SR_latch_using_NAND_gates (
  input  S,
  input  R,
  input  EN
);

  wire nand_1_p3, nand_2_p3, nand_3_p2, nand_3_p3;

  // NAND_Gate nand_1: pin names not known; wires that end beside it: S, EN, nand_1_p3
  // NAND_Gate nand_2: pin names not known; wires that end beside it: R, EN, nand_2_p3
  // NAND_Gate nand_3: pin names not known; wires that end beside it: nand_1_p3, nand_3_p2, nand_3_p3
  // NAND_Gate nand_4: pin names not known; wires that end beside it: nand_2_p3, nand_3_p3, nand_3_p2
  LED led_1 (.in(nand_3_p3));
  LED led_2 (.in(nand_3_p2));

  // Notes on the sheet:
  //   Clocked SR latch using NAND gates
  //   Clock/enable is level-sensitive.
  //   Q
  //   Qbar
endmodule

// Clocked SR latch using NOR gates
module _28_Clocked_SR_latch_using_NOR_gates (
  input  S,
  input  R,
  input  EN
);

  wire nor_1_p3, nor_2_p3, nor_3_p3, nor_4_p3, nor_5_p3, nor_6_p2, nor_6_p3;

  // NOR_Gate nor_1: pin names not known; wires that end beside it: S, S, nor_1_p3
  // NOR_Gate nor_2: pin names not known; wires that end beside it: R, R, nor_2_p3
  // NOR_Gate nor_3: pin names not known; wires that end beside it: EN, EN, nor_3_p3
  // NOR_Gate nor_4: pin names not known; wires that end beside it: nor_1_p3, nor_3_p3, nor_4_p3
  // NOR_Gate nor_5: pin names not known; wires that end beside it: nor_2_p3, nor_3_p3, nor_5_p3
  // NOR_Gate nor_6: pin names not known; wires that end beside it: nor_5_p3, nor_6_p2, nor_6_p3
  // NOR_Gate nor_7: pin names not known; wires that end beside it: nor_4_p3, nor_6_p3, nor_6_p2
  LED led_1 (.in(nor_6_p3));
  LED led_2 (.in(nor_6_p2));

  // Notes on the sheet:
  //   Clocked SR latch using NOR gates
  //   Clock/enable is level-sensitive.
  //   Q
  //   Qbar
endmodule

// SR latch using NAND gates
module _29_SR_latch_using_NAND_gates (
  input  Sbar,
  input  Rbar
);

  wire nand_1_p2, nand_1_p3;

  // NAND_Gate nand_1: pin names not known; wires that end beside it: Sbar, nand_1_p2, nand_1_p3
  // NAND_Gate nand_2: pin names not known; wires that end beside it: Rbar, nand_1_p3, nand_1_p2
  LED led_1 (.in(nand_1_p3));
  LED led_2 (.in(nand_1_p2));

  // Notes on the sheet:
  //   SR latch using NAND gates
  //   Cross-coupled latch; NAND inputs are active-low, NOR inputs are active-high.
  //   Q
  //   Qbar
endmodule

// SR latch using NOR gates
module _30_SR_latch_using_NOR_gates (
  input  S,
  input  R
);

  wire nor_1_p2, nor_1_p3;

  // NOR_Gate nor_1: pin names not known; wires that end beside it: R, nor_1_p2, nor_1_p3
  // NOR_Gate nor_2: pin names not known; wires that end beside it: S, nor_1_p3, nor_1_p2
  LED led_1 (.in(nor_1_p3));
  LED led_2 (.in(nor_1_p2));

  // Notes on the sheet:
  //   SR latch using NOR gates
  //   Cross-coupled latch; NAND inputs are active-low, NOR inputs are active-high.
  //   Q
  //   Qbar
endmodule

// 3-bit seven-segment display
module _31_3_bit_seven_segment_display (
  input  A,
  input  B,
  input  C
);

  wire and_1_out, and_2_out, and_3_out, and_4_out, and_5_out, and_6_out, and_7_out, and_8_out, and_9_out,
       and_10_out, and_11_out, and_12_out, and_13_out, and_14_out, and_15_out, and_16_out, and_17_out,
       and_18_out, and_19_out, and_20_out, and_21_out, and_22_out, and_23_out, and_24_out, and_25_out,
       and_26_out, and_27_out, and_28_out, and_29_out, and_30_out, and_31_out, and_32_out, and_33_out,
       and_34_out, and_35_out, and_36_out, and_37_out, and_38_out, and_39_out, and_40_out, and_41_out,
       and_42_out, and_43_out, and_44_out, and_45_out, and_46_out, and_47_out, and_48_out, and_49_out,
       and_50_out, and_51_out, and_52_out, and_53_out, and_54_out, and_55_out, and_56_out, and_57_out,
       and_58_out, and_59_out, and_60_out, and_61_out, and_62_out, and_63_out, and_64_out, and_65_out,
       and_66_out, and_67_out, and_68_out, and_69_out, and_70_out, and_71_out, and_72_out, not_1_out,
       not_2_out, not_3_out, not_4_out, not_5_out, not_6_out, not_7_out, not_8_out, not_9_out, not_10_out,
       not_11_out, not_12_out, not_13_out, not_14_out, not_15_out, not_16_out, not_17_out, not_18_out,
       not_19_out, not_20_out, not_21_out, not_22_out, not_23_out, not_24_out, not_25_out, not_26_out,
       not_27_out, not_28_out, not_29_out, not_30_out, not_31_out, not_32_out, not_33_out, not_34_out,
       not_35_out, not_36_out, not_37_out, not_38_out, not_39_out, not_40_out, not_41_out, not_42_out,
       not_43_out, not_44_out, not_45_out, not_46_out, not_47_out, not_48_out, not_49_out, not_50_out,
       not_51_out, not_52_out, not_53_out, not_54_out, not_55_out, not_56_out, or_1_out, or_2_out, or_3_out,
       or_4_out, or_5_out, or_6_out, or_7_out, or_8_out, or_9_out, or_10_out, or_11_out, or_12_out,
       or_13_out, or_14_out, or_15_out, or_16_out, or_17_out, or_18_out, or_19_out, or_20_out, or_21_out,
       or_22_out, or_23_out, or_24_out, or_25_out, or_26_out, or_27_out, or_28_out, or_29_out;

  not not_1 (not_1_out, A);
  not not_2 (not_2_out, B);
  not not_3 (not_3_out, C);
  not not_4 (not_4_out, A);
  not not_5 (not_5_out, C);
  not not_6 (not_6_out, A);
  not not_7 (not_7_out, B);
  not not_8 (not_8_out, C);
  and and_1 (and_1_out, A, B);
  and and_2 (and_2_out, A, B);
  not not_9 (not_9_out, A);
  not not_10 (not_10_out, B);
  not not_11 (not_11_out, C);
  not not_12 (not_12_out, A);
  not not_13 (not_13_out, B);
  not not_14 (not_14_out, A);
  not not_15 (not_15_out, C);
  not not_16 (not_16_out, A);
  not not_17 (not_17_out, B);
  not not_18 (not_18_out, C);
  and and_3 (and_3_out, A, B);
  not not_19 (not_19_out, A);
  not not_20 (not_20_out, B);
  not not_21 (not_21_out, C);
  not not_22 (not_22_out, A);
  not not_23 (not_23_out, B);
  not not_24 (not_24_out, A);
  not not_25 (not_25_out, B);
  not not_26 (not_26_out, C);
  not not_27 (not_27_out, B);
  not not_28 (not_28_out, C);
  and and_4 (and_4_out, A, B);
  and and_5 (and_5_out, A, B);
  not not_29 (not_29_out, A);
  not not_30 (not_30_out, B);
  not not_31 (not_31_out, C);
  not not_32 (not_32_out, A);
  not not_33 (not_33_out, C);
  not not_34 (not_34_out, A);
  not not_35 (not_35_out, B);
  not not_36 (not_36_out, C);
  and and_6 (and_6_out, A, B);
  not not_37 (not_37_out, A);
  not not_38 (not_38_out, B);
  not not_39 (not_39_out, C);
  not not_40 (not_40_out, A);
  not not_41 (not_41_out, C);
  not not_42 (not_42_out, C);
  and and_7 (and_7_out, A, B);
  not not_43 (not_43_out, A);
  not not_44 (not_44_out, B);
  not not_45 (not_45_out, C);
  not not_46 (not_46_out, B);
  not not_47 (not_47_out, C);
  not not_48 (not_48_out, B);
  not not_49 (not_49_out, C);
  and and_8 (and_8_out, A, B);
  not not_50 (not_50_out, A);
  not not_51 (not_51_out, C);
  not not_52 (not_52_out, A);
  not not_53 (not_53_out, B);
  not not_54 (not_54_out, C);
  not not_55 (not_55_out, B);
  not not_56 (not_56_out, C);
  and and_9 (and_9_out, A, B);
  and and_10 (and_10_out, not_1_out, not_2_out);
  and and_11 (and_11_out, not_4_out, B);
  and and_12 (and_12_out, not_6_out, B);
  and and_13 (and_13_out, A, not_7_out);
  and and_14 (and_14_out, and_1_out, not_8_out);
  and and_15 (and_15_out, and_2_out, C);
  and and_16 (and_16_out, not_9_out, not_10_out);
  and and_17 (and_17_out, not_12_out, not_13_out);
  and and_18 (and_18_out, not_14_out, B);
  and and_19 (and_19_out, not_16_out, B);
  and and_20 (and_20_out, A, not_17_out);
  and and_21 (and_21_out, and_3_out, C);
  and and_22 (and_22_out, not_19_out, not_20_out);
  and and_23 (and_23_out, not_22_out, not_23_out);
  and and_24 (and_24_out, not_24_out, B);
  and and_25 (and_25_out, A, not_25_out);
  and and_26 (and_26_out, A, not_27_out);
  and and_27 (and_27_out, and_4_out, not_28_out);
  and and_28 (and_28_out, and_5_out, C);
  and and_29 (and_29_out, not_29_out, not_30_out);
  and and_30 (and_30_out, not_32_out, B);
  and and_31 (and_31_out, not_34_out, B);
  and and_32 (and_32_out, A, not_35_out);
  and and_33 (and_33_out, and_6_out, not_36_out);
  and and_34 (and_34_out, not_37_out, not_38_out);
  and and_35 (and_35_out, not_40_out, B);
  and and_36 (and_36_out, and_7_out, not_42_out);
  and and_37 (and_37_out, not_43_out, not_44_out);
  and and_38 (and_38_out, A, not_46_out);
  and and_39 (and_39_out, A, not_48_out);
  and and_40 (and_40_out, and_8_out, not_49_out);
  and and_41 (and_41_out, not_50_out, B);
  and and_42 (and_42_out, not_52_out, B);
  and and_43 (and_43_out, A, not_53_out);
  and and_44 (and_44_out, A, not_55_out);
  and and_45 (and_45_out, and_9_out, not_56_out);
  and and_46 (and_46_out, and_10_out, not_3_out);
  and and_47 (and_47_out, and_11_out, not_5_out);
  and and_48 (and_48_out, and_12_out, C);
  and and_49 (and_49_out, and_13_out, C);
  or or_1 (or_1_out, and_14_out, and_15_out);
  and and_50 (and_50_out, and_16_out, not_11_out);
  and and_51 (and_51_out, and_17_out, C);
  and and_52 (and_52_out, and_18_out, not_15_out);
  and and_53 (and_53_out, and_19_out, C);
  and and_54 (and_54_out, and_20_out, not_18_out);
  and and_55 (and_55_out, and_22_out, not_21_out);
  and and_56 (and_56_out, and_23_out, C);
  and and_57 (and_57_out, and_24_out, C);
  and and_58 (and_58_out, and_25_out, not_26_out);
  and and_59 (and_59_out, and_26_out, C);
  and and_60 (and_60_out, and_29_out, not_31_out);
  and and_61 (and_61_out, and_30_out, not_33_out);
  and and_62 (and_62_out, and_31_out, C);
  and and_63 (and_63_out, and_32_out, C);
  and and_64 (and_64_out, and_34_out, not_39_out);
  and and_65 (and_65_out, and_35_out, not_41_out);
  and and_66 (and_66_out, and_37_out, not_45_out);
  and and_67 (and_67_out, and_38_out, not_47_out);
  and and_68 (and_68_out, and_39_out, C);
  and and_69 (and_69_out, and_41_out, not_51_out);
  and and_70 (and_70_out, and_42_out, C);
  and and_71 (and_71_out, and_43_out, not_54_out);
  and and_72 (and_72_out, and_44_out, C);
  or or_2 (or_2_out, and_46_out, and_47_out);
  or or_3 (or_3_out, and_48_out, and_49_out);
  or or_4 (or_4_out, and_50_out, and_51_out);
  or or_5 (or_5_out, and_52_out, and_53_out);
  or or_6 (or_6_out, and_54_out, and_21_out);
  or or_7 (or_7_out, and_55_out, and_56_out);
  or or_8 (or_8_out, and_57_out, and_58_out);
  or or_9 (or_9_out, and_59_out, and_27_out);
  or or_10 (or_10_out, and_60_out, and_61_out);
  or or_11 (or_11_out, and_62_out, and_63_out);
  or or_12 (or_12_out, and_64_out, and_65_out);
  or or_13 (or_13_out, and_66_out, and_67_out);
  or or_14 (or_14_out, and_68_out, and_40_out);
  or or_15 (or_15_out, and_69_out, and_70_out);
  or or_16 (or_16_out, and_71_out, and_72_out);
  or or_17 (or_17_out, or_2_out, or_3_out);
  or or_18 (or_18_out, or_4_out, or_5_out);
  or or_19 (or_19_out, or_7_out, or_8_out);
  or or_20 (or_20_out, or_9_out, and_28_out);
  or or_21 (or_21_out, or_10_out, or_11_out);
  or or_22 (or_22_out, or_12_out, and_36_out);
  or or_23 (or_23_out, or_13_out, or_14_out);
  or or_24 (or_24_out, or_15_out, or_16_out);
  or or_25 (or_25_out, or_17_out, or_1_out);
  or or_26 (or_26_out, or_18_out, or_6_out);
  or or_27 (or_27_out, or_19_out, or_20_out);
  or or_28 (or_28_out, or_21_out, and_33_out);
  or or_29 (or_29_out, or_24_out, and_45_out);
  LED led_1 (.in(or_25_out));
  LED led_2 (.in(or_26_out));
  LED led_3 (.in(or_27_out));
  LED led_4 (.in(or_28_out));
  LED led_5 (.in(or_22_out));
  LED led_6 (.in(or_23_out));
  LED led_7 (.in(or_29_out));

  // Notes on the sheet:
  //   3-bit seven-segment display
  //   Common-cathode outputs (active-high); A is MSB and C is LSB for digits 0-7.
  //   a
  //   b
  //   c
  //   d
  //   e
  //   f
  //   g
endmodule

// XNOR gate using NAND gates
module _32_XNOR_gate_using_NAND_gates (
  input  A,
  input  B
);

  wire nand_1_p3, nand_2_p4, nand_3_p4, nand_4_p3, nand_5_p3;

  // NAND_Gate nand_1: pin names not known; wires that end beside it: A, B, nand_1_p3
  // NAND_Gate nand_2: pin names not known; wires that end beside it: A, nand_1_p3, B, nand_2_p4
  // NAND_Gate nand_3: pin names not known; wires that end beside it: nand_1_p3, B, nand_1_p3, nand_3_p4
  // NAND_Gate nand_4: pin names not known; wires that end beside it: nand_2_p4, nand_3_p4, nand_4_p3
  // NAND_Gate nand_5: pin names not known; wires that end beside it: nand_4_p3, nand_4_p3, nand_5_p3
  LED led_1 (.in(nand_5_p3));

  // Notes on the sheet:
  //   XNOR gate using NAND gates
  //   NAND implementation of Y=(A XOR B)'.
  //   Y
endmodule

// XNOR gate using NOR gates
module _33_XNOR_gate_using_NOR_gates (
  input  A,
  input  B
);

  wire nor_1_p3, nor_2_p4, nor_3_p4, nor_4_p3;

  // NOR_Gate nor_1: pin names not known; wires that end beside it: A, B, nor_1_p3
  // NOR_Gate nor_2: pin names not known; wires that end beside it: A, nor_1_p3, B, nor_2_p4
  // NOR_Gate nor_3: pin names not known; wires that end beside it: nor_1_p3, B, nor_1_p3, nor_3_p4
  // NOR_Gate nor_4: pin names not known; wires that end beside it: nor_2_p4, nor_3_p4, nor_4_p3
  LED led_1 (.in(nor_4_p3));

  // Notes on the sheet:
  //   XNOR gate using NOR gates
  //   Four-NOR XNOR network.
  //   Y
endmodule

// XOR gate using NAND gates
module _34_XOR_gate_using_NAND_gates (
  input  A,
  input  B
);

  wire nand_1_p3, nand_2_p4, nand_3_p4, nand_4_p3;

  // NAND_Gate nand_1: pin names not known; wires that end beside it: A, B, nand_1_p3
  // NAND_Gate nand_2: pin names not known; wires that end beside it: A, nand_1_p3, B, nand_2_p4
  // NAND_Gate nand_3: pin names not known; wires that end beside it: nand_1_p3, B, nand_1_p3, nand_3_p4
  // NAND_Gate nand_4: pin names not known; wires that end beside it: nand_2_p4, nand_3_p4, nand_4_p3
  LED led_1 (.in(nand_4_p3));

  // Notes on the sheet:
  //   XOR gate using NAND gates
  //   Four-NAND XOR network.
  //   Y
endmodule

// XOR gate using NOR gates
module _35_XOR_gate_using_NOR_gates (
  input  A,
  input  B
);

  wire nor_1_p3, nor_2_p4, nor_3_p4, nor_4_p3, nor_5_p3;

  // NOR_Gate nor_1: pin names not known; wires that end beside it: A, B, nor_1_p3
  // NOR_Gate nor_2: pin names not known; wires that end beside it: A, nor_1_p3, B, nor_2_p4
  // NOR_Gate nor_3: pin names not known; wires that end beside it: nor_1_p3, B, nor_1_p3, nor_3_p4
  // NOR_Gate nor_4: pin names not known; wires that end beside it: nor_2_p4, nor_3_p4, nor_4_p3
  // NOR_Gate nor_5: pin names not known; wires that end beside it: nor_4_p3, nor_4_p3, nor_5_p3
  LED led_1 (.in(nor_5_p3));

  // Notes on the sheet:
  //   XOR gate using NOR gates
  //   NOR-only XOR network.
  //   Y
endmodule

// AND gate
module _36_AND_gate (
  input  A,
  input  B
);

  wire and_1_out;

  and and_1 (and_1_out, A, B);
  LED led_1 (.in(and_1_out));

  // Notes on the sheet:
  //   AND gate
  //   Y
endmodule

// OR gate
module _37_OR_gate (
  input  A,
  input  B
);

  wire or_1_out;

  or or_1 (or_1_out, A, B);
  LED led_1 (.in(or_1_out));

  // Notes on the sheet:
  //   OR gate
  //   Y
endmodule

// NOT gate
module _38_NOT_gate (
  input  A
);

  wire not_1_out;

  not not_1 (not_1_out, A);
  LED led_1 (.in(not_1_out));

  // Notes on the sheet:
  //   NOT gate
  //   Y
endmodule

// XOR gate
module _39_XOR_gate (
  input  A,
  input  B
);

  wire xor_1_p3;

  // XOR_Gate xor_1: pin names not known; wires that end beside it: A, B, xor_1_p3
  LED led_1 (.in(xor_1_p3));

  // Notes on the sheet:
  //   XOR gate
  //   Y
endmodule

// XNOR gate
module _40_XNOR_gate (
  input  A,
  input  B
);

  wire xnor_1_out;

  xnor xnor_1 (xnor_1_out, A, B);
  LED led_1 (.in(xnor_1_out));

  // Notes on the sheet:
  //   XNOR gate
  //   Y
endmodule

// NOR gate
module _41_NOR_gate (
  input  A,
  input  B
);

  wire nor_1_p3;

  // NOR_Gate nor_1: pin names not known; wires that end beside it: A, B, nor_1_p3
  LED led_1 (.in(nor_1_p3));

  // Notes on the sheet:
  //   NOR gate
  //   Y
endmodule

// NAND gate
module _42_NAND_gate (
  input  A,
  input  B
);

  wire nand_1_p3;

  // NAND_Gate nand_1: pin names not known; wires that end beside it: A, B, nand_1_p3
  LED led_1 (.in(nand_1_p3));

  // Notes on the sheet:
  //   NAND gate
  //   Y
endmodule

// T flip-flop using NAND gates
module _43_T_flip_flop_using_NAND_gates (
  input  T,
  input  CLK
);

  wire nand_1_p3, nand_2_p3, nand_2_p4, nand_3_p3, nand_3_p4, nand_4_p2, nand_4_p3, nand_6_p3, nand_7_p3;

  // NAND_Gate nand_1: pin names not known; wires that end beside it: CLK, CLK, nand_1_p3
  // NAND_Gate nand_2: pin names not known; wires that end beside it: T, CLK, nand_2_p3, nand_2_p4
  // NAND_Gate nand_3: pin names not known; wires that end beside it: T, CLK, nand_3_p3, nand_3_p4
  // NAND_Gate nand_4: pin names not known; wires that end beside it: nand_2_p4, nand_4_p2, nand_4_p3
  // NAND_Gate nand_5: pin names not known; wires that end beside it: nand_3_p4, nand_4_p3, nand_4_p2
  // NAND_Gate nand_6: pin names not known; wires that end beside it: nand_4_p3, nand_1_p3, nand_6_p3
  // NAND_Gate nand_7: pin names not known; wires that end beside it: nand_4_p2, nand_1_p3, nand_7_p3
  // NAND_Gate nand_8: pin names not known; wires that end beside it: nand_6_p3, nand_2_p3, nand_3_p3
  // NAND_Gate nand_9: pin names not known; wires that end beside it: nand_7_p3, nand_3_p3, nand_2_p3
  LED led_1 (.in(nand_3_p3));
  LED led_2 (.in(nand_2_p3));

  // Notes on the sheet:
  //   T flip-flop using NAND gates
  //   T=1 toggles; T=0 holds. Falling-edge master-slave implementation.
  //   Q
  //   Qbar
endmodule

// F(A,B,C) = A'B + BC' + AC
module _44_F_A_B_C_A_B_BC_AC (
  input  A,
  input  B,
  input  C
);

  wire nor_1_p4, nor_2_p5, nor_3_p4, nor_4_p4, nor_5_p5, nor_6_p4, nor_7_p4, nor_8_p4, nor_9_p3;

  // NOR_Gate nor_1: pin names not known; wires that end beside it: B, B, C, nor_1_p4
  // NOR_Gate nor_2: pin names not known; wires that end beside it: B, C, C, A, nor_2_p5
  // NOR_Gate nor_3: pin names not known; wires that end beside it: C, A, A, nor_3_p4
  // NOR_Gate nor_4: pin names not known; wires that end beside it: A, nor_1_p4, nor_1_p4, nor_4_p4
  // NOR_Gate nor_5: pin names not known; wires that end beside it: nor_1_p4, nor_1_p4, C, nor_3_p4, nor_5_p5
  // NOR_Gate nor_6: pin names not known; wires that end beside it: C, nor_3_p4, nor_2_p5, nor_6_p4
  // NOR_Gate nor_7: pin names not known; wires that end beside it: nor_4_p4, nor_5_p5, nor_6_p4, nor_7_p4
  // NOR_Gate nor_8: pin names not known; wires that end beside it: nor_5_p5, nor_6_p4, nor_6_p4, nor_8_p4
  // NOR_Gate nor_9: pin names not known; wires that end beside it: nor_7_p4, nor_8_p4, nor_9_p3
  LED led_1 (.in(nor_9_p3));

  // Notes on the sheet:
  //   F(A,B,C) = A'B + BC' + AC
  //   Representative expression used because the index page does not specify F.
  //   F
endmodule

// F(A,B,C,D) = A'B + CD' + AB'D
module _45_F_A_B_C_D_A_B_CD_AB_D (
  input  A,
  input  B,
  input  C,
  input  D
);

  wire and_1_out, and_2_out, and_3_out, and_4_out, not_1_out, not_2_out, not_3_out, or_1_out, or_2_out;

  not not_1 (not_1_out, A);
  not not_2 (not_2_out, B);
  not not_3 (not_3_out, D);
  and and_1 (and_1_out, not_1_out, B);
  and and_2 (and_2_out, C, not_3_out);
  and and_3 (and_3_out, A, not_2_out);
  and and_4 (and_4_out, and_3_out, D);
  or or_1 (or_1_out, and_1_out, and_2_out);
  or or_2 (or_2_out, or_1_out, and_4_out);
  LED led_1 (.in(or_2_out));

  // Notes on the sheet:
  //   F(A,B,C,D) = A'B + CD' + AB'D
  //   Representative expression used because the index page does not specify F.
  //   F
endmodule

// F(A,B,C,D) = A'B + CD' + AB'D
module _46_F_A_B_C_D_A_B_CD_AB_D (
  input  A,
  input  B,
  input  C,
  input  D
);

  wire nand_1_p4, nand_2_p5, nand_3_p4, nand_4_p4, nand_5_p5, nand_6_p4, nand_7_p4, nand_8_p4, nand_9_p4,
       nand_10_p4, nand_11_p3;

  // NAND_Gate nand_1: pin names not known; wires that end beside it: A, A, B, nand_1_p4
  // NAND_Gate nand_2: pin names not known; wires that end beside it: A, B, B, D, nand_2_p5
  // NAND_Gate nand_3: pin names not known; wires that end beside it: B, D, D, nand_3_p4
  // NAND_Gate nand_4: pin names not known; wires that end beside it: nand_1_p4, B, C, nand_4_p4
  // NAND_Gate nand_5: pin names not known; wires that end beside it: B, C, nand_3_p4, A, nand_5_p5
  // NAND_Gate nand_6: pin names not known; wires that end beside it: nand_3_p4, A, nand_2_p5, nand_6_p4
  // NAND_Gate nand_7: pin names not known; wires that end beside it: nand_6_p4, nand_6_p4, nand_4_p4, nand_7_p4
  // NAND_Gate nand_8: pin names not known; wires that end beside it: nand_6_p4, nand_4_p4, nand_5_p5, nand_8_p4
  // NAND_Gate nand_9: pin names not known; wires that end beside it: nand_7_p4, D, nand_8_p4, nand_9_p4
  // NAND_Gate nand_10: pin names not known; wires that end beside it: D, nand_8_p4, nand_8_p4, nand_10_p4
  // NAND_Gate nand_11: pin names not known; wires that end beside it: nand_10_p4, nand_9_p4, nand_11_p3
  LED led_1 (.in(nand_11_p3));

  // Notes on the sheet:
  //   F(A,B,C,D) = A'B + CD' + AB'D
  //   Representative expression used because the index page does not specify F.
  //   F
endmodule

// NOT gate using NAND gate
module _47_NOT_gate_using_NAND_gate (
  input  A
);

  wire nand_1_p3;

  // NAND_Gate nand_1: pin names not known; wires that end beside it: A, A, nand_1_p3
  LED led_1 (.in(nand_1_p3));

  // Notes on the sheet:
  //   NOT gate using NAND gate
  //   Tie both NAND inputs to A.
  //   Y
endmodule

// NOT gate using NOR gate
module _48_NOT_gate_using_NOR_gate (
  input  A
);

  wire nor_1_p3;

  // NOR_Gate nor_1: pin names not known; wires that end beside it: A, A, nor_1_p3
  LED led_1 (.in(nor_1_p3));

  // Notes on the sheet:
  //   NOT gate using NOR gate
  //   Tie both NOR inputs to A.
  //   Y
endmodule

// F(A,B) = A'B + AB'
module _49_F_A_B_A_B_AB (
  input  A,
  input  B
);

  wire and_1_out, and_2_out, not_1_out, not_2_out, or_1_out;

  not not_1 (not_1_out, A);
  not not_2 (not_2_out, B);
  and and_1 (and_1_out, not_1_out, B);
  and and_2 (and_2_out, A, not_2_out);
  or or_1 (or_1_out, and_1_out, and_2_out);
  LED led_1 (.in(or_1_out));

  // Notes on the sheet:
  //   F(A,B) = A'B + AB'
  //   Representative two-variable expression; equals A XOR B.
  //   F
endmodule

// F(A,B) = A'B + AB'
module _50_F_A_B_A_B_AB (
  input  A,
  input  B
);

  wire nand_1_p3, nand_2_p4, nand_3_p4, nand_4_p3;

  // NAND_Gate nand_1: pin names not known; wires that end beside it: A, B, nand_1_p3
  // NAND_Gate nand_2: pin names not known; wires that end beside it: A, nand_1_p3, B, nand_2_p4
  // NAND_Gate nand_3: pin names not known; wires that end beside it: nand_1_p3, B, nand_1_p3, nand_3_p4
  // NAND_Gate nand_4: pin names not known; wires that end beside it: nand_2_p4, nand_3_p4, nand_4_p3
  LED led_1 (.in(nand_4_p3));

  // Notes on the sheet:
  //   F(A,B) = A'B + AB'
  //   NAND-only realization of the representative two-variable expression.
  //   F
endmodule
