// Logisim project DEE_Lab_All_50_Circuits.circ as structural Verilog: 50 circuits, main circuit C01_1x4_Demultiplexer
module C01_1x4_Demultiplexer (
  input  S1,
  input  S0,
  input  D,
  output Y0,
  output Y1,
  output Y2,
  output Y3
);

  wire not_1_out, not_2_out, undriven, undriven_2, undriven_3, undriven_4, undriven_5, undriven_6,
       undriven_7, undriven_8, undriven_9;

  not not_1 (not_1_out, undriven);
  not not_2 (not_2_out, undriven_3);
  and and_1 (Y3, D, S1, S0);
  and and_2 (Y0, undriven_5, undriven_8, undriven_9);
  and and_3 (Y1, undriven_6, not_1_out, undriven_4);
  and and_4 (Y2, undriven_7, undriven_2, not_2_out);

  // Notes on the sheet:
  //   1. 1x4 Demultiplexer
  //   Y0..Y3: D is routed to the output selected by S1 S0
  //   Toggle the input pins with the Poke tool (hand icon); the output pins show the result.
endmodule

module C02_2x4_Decoder (
  input  A,
  input  B,
  output D0,
  output D1,
  output D2,
  output D3
);

  wire not_1_out, not_2_out, undriven, undriven_2, undriven_3, undriven_4, undriven_5, undriven_6;

  not not_1 (not_1_out, undriven);
  not not_2 (not_2_out, undriven_3);
  and and_1 (D3, A, B);
  and and_2 (D0, undriven_5, undriven_6);
  and and_3 (D1, not_1_out, undriven_4);
  and and_4 (D2, undriven_2, not_2_out);

  // Notes on the sheet:
  //   2. 2x4 Decoder
  //   D0 = A'B', D1 = A'B, D2 = AB', D3 = AB
  //   Toggle the input pins with the Poke tool (hand icon); the output pins show the result.
endmodule

module C03_3x8_Decoder (
  input  A,
  input  B,
  input  C,
  output D0,
  output D1,
  output D2,
  output D3,
  output D4,
  output D5,
  output D6,
  output D7
);

  wire not_1_out, not_2_out, not_3_out, undriven, undriven_2, undriven_3, undriven_4, undriven_5, undriven_6,
       undriven_7, undriven_8, undriven_9, undriven_10, undriven_11, undriven_12, undriven_13, undriven_14,
       undriven_15, undriven_16, undriven_17, undriven_18, undriven_19, undriven_20, undriven_21;

  not not_1 (not_1_out, undriven);
  not not_2 (not_2_out, undriven_5);
  not not_3 (not_3_out, undriven_9);
  and and_1 (D7, A, B, C);
  and and_2 (D0, undriven_13, undriven_16, undriven_19);
  and and_3 (D1, undriven_14, undriven_17, undriven_10);
  and and_4 (D2, undriven_15, undriven_6, undriven_20);
  and and_5 (D3, not_1_out, undriven_7, undriven_11);
  and and_6 (D4, undriven_2, undriven_18, undriven_21);
  and and_7 (D5, undriven_3, not_2_out, undriven_12);
  and and_8 (D6, undriven_4, undriven_8, not_3_out);

  // Notes on the sheet:
  //   3. 3x8 Decoder
  //   Dk = minterm k of A B C
  //   Toggle the input pins with the Poke tool (hand icon); the output pins show the result.
endmodule

module C04_4x1_Multiplexer (
  input  S1,
  input  S0,
  input  I0,
  input  I1,
  input  I2,
  input  I3,
  output Y
);

  wire and_1_out, and_2_out, and_3_out, and_4_out, not_1_out, not_2_out, undriven, undriven_2, undriven_3,
       undriven_4, undriven_5, undriven_6;

  not not_1 (not_1_out, undriven);
  not not_2 (not_2_out, undriven_3);
  and and_1 (and_1_out, I3, S1, S0);
  and and_2 (and_2_out, I0, undriven_5, undriven_6);
  and and_3 (and_3_out, I1, not_1_out, undriven_4);
  and and_4 (and_4_out, I2, undriven_2, not_2_out);
  or or_1 (Y, and_2_out, and_3_out, and_4_out, and_1_out);

  // Notes on the sheet:
  //   4. 4x1 Multiplexer
  //   Y = I(S1S0): selects one of I0..I3
  //   Toggle the input pins with the Poke tool (hand icon); the output pins show the result.
endmodule

module C05_8x1_Multiplexer (
  input  S2,
  input  S1,
  input  S0,
  input  I0,
  input  I1,
  input  I2,
  input  I3,
  input  I4,
  input  I5,
  input  I6,
  input  I7,
  output Y
);

  wire and_1_out, and_2_out, and_3_out, and_4_out, and_5_out, and_6_out, and_7_out, and_8_out, not_1_out,
       not_2_out, not_3_out, undriven, undriven_2, undriven_3, undriven_4, undriven_5, undriven_6,
       undriven_7, undriven_8, undriven_9, undriven_10, undriven_11, undriven_12, undriven_13, undriven_14,
       undriven_15, undriven_16, undriven_17, undriven_18, undriven_19, undriven_20, undriven_21;

  not not_1 (not_1_out, undriven);
  not not_2 (not_2_out, undriven_5);
  not not_3 (not_3_out, undriven_9);
  and and_1 (and_1_out, I7, S2, S1, S0);
  and and_2 (and_2_out, I0, undriven_13, undriven_16, undriven_19);
  and and_3 (and_3_out, I1, undriven_14, undriven_17, undriven_10);
  and and_4 (and_4_out, I2, undriven_15, undriven_6, undriven_20);
  and and_5 (and_5_out, I3, not_1_out, undriven_7, undriven_11);
  and and_6 (and_6_out, I4, undriven_2, undriven_18, undriven_21);
  and and_7 (and_7_out, I5, undriven_3, not_2_out, undriven_12);
  and and_8 (and_8_out, I6, undriven_4, undriven_8, not_3_out);
  or or_1 (Y, and_2_out, and_3_out, and_4_out, and_5_out, and_6_out, and_7_out, and_8_out, and_1_out);

  // Notes on the sheet:
  //   5. 8x1 Multiplexer
  //   Y = I(S2S1S0): selects one of I0..I7
  //   Toggle the input pins with the Poke tool (hand icon); the output pins show the result.
endmodule

module C06_Octal_to_Binary_Encoder (
  input  D4,
  input  D5,
  input  D6,
  input  D7,
  input  D2,
  input  D3,
  input  D1,
  input  D0,
  output A2,
  output A1,
  output A0
);

  wire undriven, undriven_2, undriven_3, undriven_4, undriven_5;

  or or_1 (A2, D4, undriven, undriven_2, undriven_3);
  or or_2 (A1, D2, undriven_5, D6, undriven_4);
  or or_3 (A0, D1, D3, D5, D7);

  // Notes on the sheet:
  //   6. Octal to Binary Encoder (8:3)
  //   A2 = D4+D5+D6+D7, A1 = D2+D3+D6+D7, A0 = D1+D3+D5+D7
  //   Toggle the input pins with the Poke tool (hand icon); the output pins show the result.
endmodule

module C07_Decimal_to_BCD_Encoder (
  input  D8,
  input  D9,
  input  D4,
  input  D5,
  input  D6,
  input  D7,
  input  D2,
  input  D3,
  input  D1,
  input  D0,
  output A3,
  output A2,
  output A1,
  output A0
);

  wire undriven, undriven_2, undriven_3, undriven_4, undriven_5, undriven_6;

  or or_1 (A3, D8, undriven);
  or or_2 (A2, D4, undriven_2, undriven_3, undriven_4);
  or or_3 (A1, D2, undriven_6, D6, undriven_5);
  or or_4 (A0, D1, D3, D5, D7, D9);

  // Notes on the sheet:
  //   7. Decimal to BCD Encoder (10:4)
  //   A3 = D8+D9, A2 = D4..D7, A1 = D2+D3+D6+D7, A0 = D1+D3+D5+D7+D9
  //   Toggle the input pins with the Poke tool (hand icon); the output pins show the result.
endmodule

module C08_2x1_Multiplexer (
  input  S,
  input  I0,
  input  I1,
  output Y
);

  wire and_1_out, and_2_out, not_1_out, undriven;

  not not_1 (not_1_out, undriven);
  and and_1 (and_1_out, I1, S);
  and and_2 (and_2_out, I0, not_1_out);
  or or_1 (Y, and_2_out, and_1_out);

  // Notes on the sheet:
  //   8. 2x1 Multiplexer
  //   Y = S'.I0 + S.I1
  //   Toggle the input pins with the Poke tool (hand icon); the output pins show the result.
endmodule

module C09_3bit_Even_Parity_Generator_NAND (
  input  A,
  input  B,
  input  C,
  output P
);

  wire nand_1_out, nand_2_out, nand_3_out, nand_4_out, nand_5_out, nand_6_out, nand_7_out, undriven,
       undriven_2, undriven_3, undriven_4, undriven_5, undriven_6;

  nand nand_1 (nand_1_out, undriven, undriven_2);
  nand nand_2 (nand_2_out, A, undriven_4);
  nand nand_3 (nand_3_out, B, nand_1_out);
  nand nand_4 (nand_4_out, nand_2_out, nand_3_out);
  nand nand_5 (nand_5_out, undriven_5, undriven_3);
  nand nand_6 (nand_6_out, nand_4_out, undriven_6);
  nand nand_7 (nand_7_out, C, nand_5_out);
  nand nand_8 (P, nand_6_out, nand_7_out);

  // Notes on the sheet:
  //   9. 3-bit Even Parity Generator (NAND)
  //   P = A xor B xor C built from 8 NAND gates
  //   Toggle the input pins with the Poke tool (hand icon); the output pins show the result.
endmodule

module C10_4bit_Even_Parity_Generator_NAND (
  input  A,
  input  B,
  input  C,
  input  D,
  output P
);

  wire nand_1_out, nand_2_out, nand_3_out, nand_4_out, nand_5_out, nand_6_out, nand_7_out, nand_8_out,
       nand_9_out, nand_10_out, nand_11_out, undriven, undriven_2, undriven_3, undriven_4, undriven_5,
       undriven_6, undriven_7, undriven_8, undriven_9;

  nand nand_1 (nand_1_out, undriven, undriven_2);
  nand nand_2 (nand_2_out, A, undriven_5);
  nand nand_3 (nand_3_out, B, nand_1_out);
  nand nand_4 (nand_4_out, nand_2_out, nand_3_out);
  nand nand_5 (nand_5_out, undriven_6, undriven_3);
  nand nand_6 (nand_6_out, nand_4_out, undriven_7);
  nand nand_7 (nand_7_out, C, nand_5_out);
  nand nand_8 (nand_8_out, nand_6_out, nand_7_out);
  nand nand_9 (nand_9_out, undriven_8, undriven_4);
  nand nand_10 (nand_10_out, nand_8_out, undriven_9);
  nand nand_11 (nand_11_out, D, nand_9_out);
  nand nand_12 (P, nand_10_out, nand_11_out);

  // Notes on the sheet:
  //   10. 4-bit Even Parity Generator (NAND)
  //   P = A xor B xor C xor D built from 12 NAND gates
  //   Toggle the input pins with the Poke tool (hand icon); the output pins show the result.
endmodule

module C11_AND_using_NAND (
  input  A,
  input  B,
  output Y
);

  wire nand_1_out, undriven;

  nand nand_1 (nand_1_out, A, B);
  nand nand_2 (Y, undriven, nand_1_out);

  // Notes on the sheet:
  //   11. AND gate using NAND gates
  //   Y = ((A.B)')' (2 NAND gates)
  //   Toggle the input pins with the Poke tool (hand icon); the output pins show the result.
endmodule

module C12_AND_using_NOR (
  input  A,
  input  B,
  output Y
);

  wire nor_1_out, nor_2_out, undriven, undriven_2;

  nor nor_1 (nor_1_out, undriven, A);
  nor nor_2 (nor_2_out, undriven_2, B);
  nor nor_3 (Y, nor_1_out, nor_2_out);

  // Notes on the sheet:
  //   12. AND gate using NOR gates
  //   Y = A' NOR B' (3 NOR gates)
  //   Toggle the input pins with the Poke tool (hand icon); the output pins show the result.
endmodule

module C13_D_Flip_Flop_NAND (
  input  D,
  input  CLK,
  input  CLR_bar,
  output Q,
  output Q_bar
);

  wire nand_1_out, nand_2_out, nand_3_out, nand_4_out, nand_5_out, undriven, undriven_2, undriven_3,
       undriven_4;

  nand nand_1 (nand_1_out, undriven, undriven_2);
  nand nand_2 (nand_2_out, D, undriven_3, undriven_4);
  nand nand_3 (nand_3_out, nand_1_out, CLK);
  nand nand_4 (nand_4_out, nand_3_out, CLR_bar, nand_5_out);
  nand nand_5 (nand_5_out, nand_2_out, Q_bar);

  // Notes on the sheet:
  //   13. D Flip-Flop using NAND gates
  //   Q follows D while CLK = 1 and holds when CLK = 0 (CLR_bar = 0 clears Q)
  //   CLR_bar=0 holds Q=0 (start state). Set CLR_bar=1; while CLK=1 Q follows D; set CLK=0 to hold the value.
endmodule

module C14_Excess3_from_BCD (
  input  B2,
  input  B1,
  input  B0,
  input  B3,
  output E0,
  output E3,
  output E2,
  output E1
);

  wire and_1_out, and_2_out, and_3_out, and_4_out, and_5_out, not_1_out, not_2_out, not_3_out, undriven,
       undriven_2, undriven_3, undriven_4, undriven_5, undriven_6, undriven_7, undriven_8, undriven_9,
       undriven_10;

  not not_1 (not_1_out, undriven);
  not not_2 (not_2_out, undriven_4);
  not not_3 (not_3_out, undriven_7);
  and and_1 (and_1_out, undriven_2, undriven_5);
  and and_2 (and_2_out, undriven_3, undriven_8);
  xnor xnor_1 (E1, B1, B0);
  or or_1 (E3, B3, and_1_out, and_2_out);
  and and_3 (and_3_out, undriven_10, undriven_6);
  and and_4 (and_4_out, not_1_out, undriven_9);
  and and_5 (and_5_out, B2, not_2_out, not_3_out);
  or or_2 (E2, and_3_out, and_4_out, and_5_out);

  // Notes on the sheet:
  //   14. Excess-3 code from BCD
  //   E3=B3+B2B1+B2B0, E2=B2'B1+B2'B0+B2B1'B0', E1=B1 XNOR B0, E0=B0'
  //   Toggle the input pins with the Poke tool (hand icon); the output pins show the result.
endmodule

module C15_Full_Adder (
  input  A,
  input  B,
  input  Cin,
  output Sum,
  output Cout
);

  wire and_1_out, and_2_out, undriven, undriven_2, undriven_3, undriven_4, xor_1_out;

  xor xor_1 (xor_1_out, undriven, undriven_2);
  and and_1 (and_1_out, A, B);
  xor xor_2 (Sum, undriven_4, undriven_3);
  and and_2 (and_2_out, xor_1_out, Cin);
  or or_1 (Cout, and_1_out, and_2_out);

  // Notes on the sheet:
  //   15. Full Adder
  //   Sum = A xor B xor Cin, Cout = AB + Cin(A xor B)
  //   Toggle the input pins with the Poke tool (hand icon); the output pins show the result.
endmodule

module C16_Full_Subtractor (
  input  A,
  input  B,
  input  Bin,
  output Diff,
  output Bout
);

  wire and_1_out, and_2_out, not_1_out, undriven, undriven_2, undriven_3, undriven_4, undriven_5, xnor_1_out,
       xor_1_out;

  xor xor_1 (xor_1_out, undriven, undriven_3);
  not not_1 (not_1_out, undriven_2);
  xnor xnor_1 (xnor_1_out, A, undriven_4);
  xor xor_2 (Diff, xor_1_out, undriven_5);
  and and_1 (and_1_out, not_1_out, B);
  and and_2 (and_2_out, xnor_1_out, Bin);
  or or_1 (Bout, and_1_out, and_2_out);

  // Notes on the sheet:
  //   16. Full Subtractor
  //   Diff = A xor B xor Bin, Bout = A'B + (A xnor B)Bin
  //   Toggle the input pins with the Poke tool (hand icon); the output pins show the result.
endmodule

module C17_Half_Adder (
  input  A,
  input  B,
  output Sum,
  output Carry
);

  wire undriven, undriven_2;

  xor xor_1 (Sum, undriven, undriven_2);
  and and_1 (Carry, A, B);

  // Notes on the sheet:
  //   17. Half Adder
  //   Sum = A xor B, Carry = AB
  //   Toggle the input pins with the Poke tool (hand icon); the output pins show the result.
endmodule

module C18_Half_Subtractor (
  input  A,
  input  B,
  output Diff,
  output Borrow
);

  wire not_1_out, undriven, undriven_2;

  not not_1 (not_1_out, undriven);
  xor xor_1 (Diff, A, undriven_2);
  and and_1 (Borrow, not_1_out, B);

  // Notes on the sheet:
  //   18. Half Subtractor
  //   Diff = A xor B, Borrow = A'B
  //   Toggle the input pins with the Poke tool (hand icon); the output pins show the result.
endmodule

module C19_3var_Expression_Basic_Gates (
  input  A,
  input  B,
  input  C,
  output F
);

  wire and_1_out, and_2_out, not_1_out, undriven;

  not not_1 (not_1_out, undriven);
  and and_1 (and_1_out, A, B);
  and and_2 (and_2_out, not_1_out, C);
  or or_1 (F, and_1_out, and_2_out);

  // Notes on the sheet:
  //   19. 3-variable expression using basic gates
  //   F = AB + A'C  (example expression)
  //   Toggle the input pins with the Poke tool (hand icon); the output pins show the result.
endmodule

module C20_3var_Expression_NAND (
  input  A,
  input  B,
  input  C,
  output F
);

  wire nand_1_out, nand_2_out, nand_3_out, undriven, undriven_2;

  nand nand_1 (nand_1_out, undriven, undriven_2);
  nand nand_2 (nand_2_out, A, B);
  nand nand_3 (nand_3_out, nand_1_out, C);
  nand nand_4 (F, nand_2_out, nand_3_out);

  // Notes on the sheet:
  //   20. 3-variable expression using NAND gates
  //   F = AB + A'C = ((AB)'.(A'C)')'  (example expression)
  //   Toggle the input pins with the Poke tool (hand icon); the output pins show the result.
endmodule

module C21_JK_Flip_Flop_NAND (
  input  CLK,
  input  J,
  input  K,
  input  CLR_bar,
  output Q,
  output Q_bar
);

  wire nand_1_out, nand_2_out, nand_3_out, nand_4_out, nand_5_out, nand_6_out, nand_7_out, nand_8_out,
       nand_9_out, undriven, undriven_2, undriven_3, undriven_4, undriven_5, undriven_6, undriven_7,
       undriven_8, undriven_9;

  nand nand_1 (nand_1_out, undriven, undriven_2);
  nand nand_2 (nand_2_out, nand_9_out, undriven_8);
  nand nand_3 (nand_3_out, nand_2_out, undriven_6);
  nand nand_4 (nand_4_out, nand_3_out, undriven_9);
  nand nand_5 (nand_5_out, K, CLK, undriven_7);
  nand nand_6 (nand_6_out, nand_5_out, undriven_4, undriven_5);
  nand nand_7 (nand_7_out, undriven_8, nand_1_out);
  nand nand_8 (nand_8_out, nand_7_out, CLR_bar, undriven_7);
  nand nand_9 (nand_9_out, J, undriven_3, Q_bar);

  // Notes on the sheet:
  //   21. JK Flip-Flop using NAND gates
  //   Master-slave JK (9 NAND gates): master loads while CLK=1, Q updates when CLK falls to 0
  //   CLR_bar=0 holds Q=0 (start state). Set CLR_bar=1, choose J,K, then toggle CLK 0->1->0: Q updates when CLK falls.
endmodule

module C22_Hexadecimal_to_Binary_Encoder (
  input  D8,
  input  D9,
  input  DA,
  input  DB,
  input  DC,
  input  DD,
  input  DE,
  input  DF,
  input  D4,
  input  D5,
  input  D6,
  input  D7,
  input  D2,
  input  D3,
  input  D1,
  input  D0,
  output A3,
  output A2,
  output A1,
  output A0
);

  wire undriven, undriven_2, undriven_3, undriven_4, undriven_5, undriven_6, undriven_7, undriven_8,
       undriven_9, undriven_10, undriven_11, undriven_12, undriven_13, undriven_14, undriven_15, undriven_16,
       undriven_17;

  or or_1 (A3, D8, undriven, undriven_2, undriven_3, undriven_5, undriven_6, undriven_8, undriven_10);
  or or_2 (A2, D4, undriven_13, undriven_14, undriven_15, DC, undriven_7, undriven_9, undriven_11);
  or or_3 (A1, D2, undriven_17, D6, undriven_16, DA, undriven_4, DE, undriven_12);
  or or_4 (A0, D1, D3, D5, D7, D9, DB, DD, DF);

  // Notes on the sheet:
  //   22. Hexadecimal to Binary Encoder (16:4)
  //   A3..A0 = binary code of the active input D0..DF
  //   Toggle the input pins with the Poke tool (hand icon); the output pins show the result.
endmodule

module C23_NAND_using_NOR (
  input  A,
  input  B,
  output Y
);

  wire nor_1_out, nor_2_out, nor_3_out, undriven, undriven_2, undriven_3;

  nor nor_1 (nor_1_out, undriven, A);
  nor nor_2 (nor_2_out, undriven_2, B);
  nor nor_3 (nor_3_out, nor_1_out, nor_2_out);
  nor nor_4 (Y, undriven_3, nor_3_out);

  // Notes on the sheet:
  //   23. NAND gate using NOR gates
  //   Y = (A.B)' (5 NOR gates)
  //   Toggle the input pins with the Poke tool (hand icon); the output pins show the result.
endmodule

module C24_NOR_using_NAND (
  input  A,
  input  B,
  output Y
);

  wire nand_1_out, nand_2_out, nand_3_out, undriven, undriven_2, undriven_3;

  nand nand_1 (nand_1_out, undriven, A);
  nand nand_2 (nand_2_out, undriven_2, B);
  nand nand_3 (nand_3_out, nand_1_out, nand_2_out);
  nand nand_4 (Y, undriven_3, nand_3_out);

  // Notes on the sheet:
  //   24. NOR gate using NAND gates
  //   Y = (A+B)' (5 NAND gates)
  //   Toggle the input pins with the Poke tool (hand icon); the output pins show the result.
endmodule

module C25_OR_using_NAND (
  input  A,
  input  B,
  output Y
);

  wire nand_1_out, nand_2_out, undriven, undriven_2;

  nand nand_1 (nand_1_out, undriven, A);
  nand nand_2 (nand_2_out, undriven_2, B);
  nand nand_3 (Y, nand_1_out, nand_2_out);

  // Notes on the sheet:
  //   25. OR gate using NAND gates
  //   Y = A' NAND B' = A + B (3 NAND gates)
  //   Toggle the input pins with the Poke tool (hand icon); the output pins show the result.
endmodule

module C26_OR_using_NOR (
  input  A,
  input  B,
  output Y
);

  wire nor_1_out, undriven;

  nor nor_1 (nor_1_out, A, B);
  nor nor_2 (Y, undriven, nor_1_out);

  // Notes on the sheet:
  //   26. OR gate using NOR gates
  //   Y = ((A+B)')' (2 NOR gates)
  //   Toggle the input pins with the Poke tool (hand icon); the output pins show the result.
endmodule

module C27_SR_Flip_Flop_NAND (
  input  S,
  input  CLK,
  input  CLR_bar,
  input  R,
  output Q,
  output Q_bar
);

  wire nand_1_out, nand_2_out, nand_3_out, nand_4_out, undriven, undriven_2;

  nand nand_1 (nand_1_out, S, undriven, undriven_2);
  nand nand_2 (nand_2_out, R, CLK);
  nand nand_3 (nand_3_out, nand_2_out, CLR_bar, nand_4_out);
  nand nand_4 (nand_4_out, nand_1_out, Q_bar);

  // Notes on the sheet:
  //   27. SR Flip-Flop using NAND gates
  //   Clocked SR: S=1,R=0 sets; S=0,R=1 resets (CLK=1); S=R=1 forbidden; CLR_bar=0 clears Q
  //   CLR_bar=0 holds Q=0 (start state). Set CLR_bar=1; with CLK=1: S=1 sets, R=1 resets, S=R=0 holds (avoid S=R=1).
endmodule

module C28_SR_Flip_Flop_NOR (
  input  CLR_bar,
  input  S,
  input  CLK,
  input  R,
  output Q,
  output Q_bar
);

  wire and_1_out, and_2_out, nor_1_out, nor_2_out, not_1_out, undriven, undriven_2;

  not not_1 (not_1_out, undriven);
  and and_1 (and_1_out, S, undriven_2, CLR_bar);
  and and_2 (and_2_out, R, CLK);
  nor nor_1 (nor_1_out, and_1_out, nor_2_out);
  nor nor_2 (nor_2_out, and_2_out, not_1_out, Q_bar);

  // Notes on the sheet:
  //   28. SR Flip-Flop using NOR gates
  //   Clocked SR: AND gating + cross-coupled NOR latch; S=R=1 forbidden; CLR_bar=0 clears Q
  //   CLR_bar=0 holds Q=0 (start state). Set CLR_bar=1; with CLK=1: S=1 sets, R=1 resets, S=R=0 holds (avoid S=R=1).
endmodule

module C29_SR_Latch_NAND (
  input  S_bar,
  input  R_bar,
  output Q,
  output Q_bar
);

  wire nand_1_out, nand_2_out;

  nand nand_1 (nand_1_out, R_bar, nand_2_out);
  nand nand_2 (nand_2_out, S_bar, Q_bar);

  // Notes on the sheet:
  //   29. SR Latch using NAND gates
  //   Active-LOW inputs: S_bar=0 sets, R_bar=0 resets, both 1 = hold, both 0 forbidden
  //   Active-LOW inputs: S_bar=0 sets Q=1, R_bar=0 resets Q=0, both 1 = hold. Never release both 0s together.
endmodule

module C30_SR_Latch_NOR (
  input  R,
  input  S,
  output Q,
  output Q_bar
);

  wire nor_1_out, nor_2_out;

  nor nor_1 (nor_1_out, S, nor_2_out);
  nor nor_2 (nor_2_out, R, Q_bar);

  // Notes on the sheet:
  //   30. SR Latch using NOR gates
  //   Active-HIGH inputs: S=1 sets, R=1 resets, both 0 = hold, both 1 forbidden
  //   Active-HIGH inputs: S=1 sets Q=1, R=1 resets Q=0, both 0 = hold (set S or R once to start). Avoid S=R=1.
endmodule

module C31_Seven_Segment_3bit (
  input  B2,
  input  B1,
  input  B0
);

  wire and_1_out, and_2_out, and_3_out, and_4_out, and_5_out, and_6_out, and_7_out, and_8_out, not_1_out,
       not_2_out, not_3_out, or_1_out, or_2_out, or_3_out, or_4_out, or_5_out, or_6_out, or_7_out, undriven,
       undriven_2, undriven_3, undriven_4, undriven_5, undriven_6, undriven_7, undriven_8, undriven_9,
       undriven_10, undriven_11, undriven_12, undriven_13, undriven_14, undriven_15, undriven_16,
       undriven_17, undriven_18, undriven_19, undriven_20, undriven_21, undriven_22, undriven_23,
       undriven_24, undriven_25, undriven_26, undriven_27, undriven_28, undriven_29, undriven_30,
       undriven_31, undriven_32, undriven_33, undriven_34, undriven_35, undriven_36, undriven_37,
       undriven_38, undriven_39, undriven_40, undriven_41, undriven_42, undriven_43, undriven_44,
       undriven_45, undriven_46, undriven_47, undriven_48, undriven_49;

  not not_1 (not_1_out, undriven);
  not not_2 (not_2_out, undriven_5);
  not not_3 (not_3_out, undriven_9);
  and and_1 (and_1_out, B2, B1, B0);
  and and_2 (and_2_out, undriven_13, undriven_16, undriven_19);
  and and_3 (and_3_out, undriven_14, undriven_17, undriven_10);
  and and_4 (and_4_out, undriven_15, undriven_6, undriven_20);
  and and_5 (and_5_out, not_1_out, undriven_7, undriven_11);
  and and_6 (and_6_out, undriven_2, undriven_18, undriven_21);
  and and_7 (and_7_out, undriven_3, not_2_out, undriven_12);
  and and_8 (and_8_out, undriven_4, undriven_8, not_3_out);
  or or_1 (or_1_out, undriven_24, undriven_29, undriven_33, undriven_37, undriven_41, undriven_22);
  or or_2 (or_2_out, undriven_25, undriven_46, undriven_30, undriven_34, undriven_47, undriven_23);
  or or_3 (or_3_out, undriven_26, and_3_out, undriven_35, undriven_48, undriven_38, undriven_42, and_1_out);
  or or_4 (or_4_out, undriven_27, undriven_31, undriven_36, undriven_39, undriven_43);
  or or_5 (or_5_out, undriven_28, undriven_32, undriven_44);
  or or_6 (or_6_out, and_2_out, undriven_49, undriven_40, undriven_45);
  or or_7 (or_7_out, and_4_out, and_5_out, and_6_out, and_7_out, and_8_out);
  _7_Segment_Display u_7_segment_display_1 (
    .g(or_7_out), .f(or_6_out), .a(or_1_out), .b(or_2_out), .e(or_5_out), .d(or_4_out), .c(or_3_out));  // open: dp

  // Notes on the sheet:
  //   31. Seven-segment decoder (3-bit)
  //   Common-cathode segments a..g for digits 0-7 (1 = ON)
  //   Toggle B2 B1 B0 (binary 0-7) with the Poke tool; the 7-segment display shows the digit.
endmodule

module C32_XNOR_using_NAND (
  input  A,
  input  B,
  output Y
);

  wire nand_1_out, nand_2_out, nand_3_out, nand_4_out, undriven, undriven_2, undriven_3, undriven_4;

  nand nand_1 (nand_1_out, undriven, undriven_2);
  nand nand_2 (nand_2_out, A, undriven_3);
  nand nand_3 (nand_3_out, B, nand_1_out);
  nand nand_4 (nand_4_out, nand_2_out, nand_3_out);
  nand nand_5 (Y, undriven_4, nand_4_out);

  // Notes on the sheet:
  //   32. XNOR gate using NAND gates
  //   Y = (A xor B)' (5 NAND gates)
  //   Toggle the input pins with the Poke tool (hand icon); the output pins show the result.
endmodule

module C33_XNOR_using_NOR (
  input  A,
  input  B,
  output Y
);

  wire nor_1_out, nor_2_out, nor_3_out, undriven, undriven_2, undriven_3;

  nor nor_1 (nor_1_out, undriven, undriven_2);
  nor nor_2 (nor_2_out, A, undriven_3);
  nor nor_3 (nor_3_out, B, nor_1_out);
  nor nor_4 (Y, nor_2_out, nor_3_out);

  // Notes on the sheet:
  //   33. XNOR gate using NOR gates
  //   Y = AB + A'B' (4 NOR gates)
  //   Toggle the input pins with the Poke tool (hand icon); the output pins show the result.
endmodule

module C34_XOR_using_NAND (
  input  A,
  input  B,
  output Y
);

  wire nand_1_out, nand_2_out, nand_3_out, undriven, undriven_2, undriven_3;

  nand nand_1 (nand_1_out, undriven, undriven_2);
  nand nand_2 (nand_2_out, A, undriven_3);
  nand nand_3 (nand_3_out, B, nand_1_out);
  nand nand_4 (Y, nand_2_out, nand_3_out);

  // Notes on the sheet:
  //   34. XOR gate using NAND gates
  //   Y = AB' + A'B (4 NAND gates)
  //   Toggle the input pins with the Poke tool (hand icon); the output pins show the result.
endmodule

module C35_XOR_using_NOR (
  input  A,
  input  B,
  output Y
);

  wire nor_1_out, nor_2_out, nor_3_out, nor_4_out, undriven, undriven_2, undriven_3, undriven_4;

  nor nor_1 (nor_1_out, undriven, undriven_2);
  nor nor_2 (nor_2_out, A, undriven_3);
  nor nor_3 (nor_3_out, B, nor_1_out);
  nor nor_4 (nor_4_out, nor_2_out, nor_3_out);
  nor nor_5 (Y, undriven_4, nor_4_out);

  // Notes on the sheet:
  //   35. XOR gate using NOR gates
  //   Y = A xor B (5 NOR gates)
  //   Toggle the input pins with the Poke tool (hand icon); the output pins show the result.
endmodule

module C36_AND_gate (
  input  A,
  input  B,
  output Y
);

  and and_1 (Y, A, B);

  // Notes on the sheet:
  //   36. AND gate
  //   Y = A.B
  //   Toggle the input pins with the Poke tool (hand icon); the output pins show the result.
endmodule

module C37_OR_gate (
  input  A,
  input  B,
  output Y
);

  or or_1 (Y, A, B);

  // Notes on the sheet:
  //   37. OR gate
  //   Y = A+B
  //   Toggle the input pins with the Poke tool (hand icon); the output pins show the result.
endmodule

module C38_NOT_gate (
  input  A,
  output Y
);

  not not_1 (Y, A);

  // Notes on the sheet:
  //   38. NOT gate
  //   Y = A'
  //   Toggle the input pins with the Poke tool (hand icon); the output pins show the result.
endmodule

module C39_XOR_gate (
  input  A,
  input  B,
  output Y
);

  xor xor_1 (Y, A, B);

  // Notes on the sheet:
  //   39. XOR gate
  //   Y = A xor B
  //   Toggle the input pins with the Poke tool (hand icon); the output pins show the result.
endmodule

module C40_XNOR_gate (
  input  A,
  input  B,
  output Y
);

  xnor xnor_1 (Y, A, B);

  // Notes on the sheet:
  //   40. XNOR gate
  //   Y = (A xor B)'
  //   Toggle the input pins with the Poke tool (hand icon); the output pins show the result.
endmodule

module C41_NOR_gate (
  input  A,
  input  B,
  output Y
);

  nor nor_1 (Y, A, B);

  // Notes on the sheet:
  //   41. NOR gate
  //   Y = (A+B)'
  //   Toggle the input pins with the Poke tool (hand icon); the output pins show the result.
endmodule

module C42_NAND_gate (
  input  A,
  input  B,
  output Y
);

  nand nand_1 (Y, A, B);

  // Notes on the sheet:
  //   42. NAND gate
  //   Y = (A.B)'
  //   Toggle the input pins with the Poke tool (hand icon); the output pins show the result.
endmodule

module C43_T_Flip_Flop (
  input  CLK,
  input  T,
  input  CLR_bar,
  output Q,
  output Q_bar
);

  wire nand_1_out, nand_2_out, nand_3_out, nand_4_out, nand_5_out, nand_6_out, nand_7_out, nand_8_out,
       nand_9_out, undriven, undriven_2, undriven_3, undriven_4, undriven_5, undriven_6, undriven_7,
       undriven_8, undriven_9, undriven_10;

  nand nand_1 (nand_1_out, undriven, undriven_2);
  nand nand_2 (nand_2_out, nand_9_out, undriven_9);
  nand nand_3 (nand_3_out, nand_2_out, undriven_7);
  nand nand_4 (nand_4_out, nand_3_out, undriven_10);
  nand nand_5 (nand_5_out, T, CLK, undriven_8);
  nand nand_6 (nand_6_out, nand_5_out, undriven_5, undriven_6);
  nand nand_7 (nand_7_out, undriven_9, nand_1_out);
  nand nand_8 (nand_8_out, nand_7_out, CLR_bar, undriven_8);
  nand nand_9 (nand_9_out, undriven_4, undriven_3, Q_bar);

  // Notes on the sheet:
  //   43. T Flip-Flop
  //   Master-slave JK with J=K=T: T=1 toggles Q on every clock pulse, T=0 holds
  //   CLR_bar=0 holds Q=0 (start state). Set CLR_bar=1, then toggle CLK 0->1->0: with T=1 Q flips each pulse, T=0 holds.
endmodule

module C44_3var_Expression_NOR (
  input  A,
  input  B,
  input  C,
  output F
);

  wire nor_1_out, nor_2_out, nor_3_out, undriven, undriven_2;

  nor nor_1 (nor_1_out, undriven, undriven_2);
  nor nor_2 (nor_2_out, A, C);
  nor nor_3 (nor_3_out, nor_1_out, B);
  nor nor_4 (F, nor_3_out, nor_2_out);

  // Notes on the sheet:
  //   44. 3-variable expression using NOR gates
  //   F = AB + A'C = NOR( NOR(A',B), NOR(A,C) )  (example expression)
  //   Toggle the input pins with the Poke tool (hand icon); the output pins show the result.
endmodule

module C45_4var_Expression_Basic_Gates (
  input  C,
  input  A,
  input  B,
  input  D,
  output F
);

  wire and_1_out, and_2_out, not_1_out;

  not not_1 (not_1_out, C);
  and and_1 (and_1_out, A, B);
  and and_2 (and_2_out, not_1_out, D);
  or or_1 (F, and_1_out, and_2_out);

  // Notes on the sheet:
  //   45. 4-variable expression using basic gates
  //   F = AB + C'D  (example expression)
  //   Toggle the input pins with the Poke tool (hand icon); the output pins show the result.
endmodule

module C46_4var_Expression_NAND (
  input  C,
  input  A,
  input  B,
  input  D,
  output F
);

  wire nand_1_out, nand_2_out, nand_3_out, undriven;

  nand nand_1 (nand_1_out, undriven, C);
  nand nand_2 (nand_2_out, A, B);
  nand nand_3 (nand_3_out, nand_1_out, D);
  nand nand_4 (F, nand_2_out, nand_3_out);

  // Notes on the sheet:
  //   46. 4-variable expression using NAND gates
  //   F = AB + C'D = ((AB)'.(C'D)')'  (example expression)
  //   Toggle the input pins with the Poke tool (hand icon); the output pins show the result.
endmodule

module C47_NOT_using_NAND (
  input  A,
  output Y
);

  wire undriven;

  nand nand_1 (Y, undriven, A);

  // Notes on the sheet:
  //   47. NOT gate using NAND gate
  //   Y = (A.A)' = A'
  //   Toggle the input pins with the Poke tool (hand icon); the output pins show the result.
endmodule

module C48_NOT_using_NOR (
  input  A,
  output Y
);

  wire undriven;

  nor nor_1 (Y, undriven, A);

  // Notes on the sheet:
  //   48. NOT gate using NOR gate
  //   Y = (A+A)' = A'
  //   Toggle the input pins with the Poke tool (hand icon); the output pins show the result.
endmodule

module C49_2var_Expression_Basic_Gates (
  input  B,
  input  A,
  output F
);

  wire not_1_out;

  not not_1 (not_1_out, B);
  or or_1 (F, A, not_1_out);

  // Notes on the sheet:
  //   49. 2-variable expression using basic gates
  //   F = A + B'  (example expression)
  //   Toggle the input pins with the Poke tool (hand icon); the output pins show the result.
endmodule

module C50_2var_Expression_NAND (
  input  A,
  input  B,
  output F
);

  wire nand_1_out, undriven;

  nand nand_1 (nand_1_out, undriven, A);
  nand nand_2 (F, nand_1_out, B);

  // Notes on the sheet:
  //   50. 2-variable expression using NAND gates
  //   F = A + B' = (A'.B)'  (example expression)
  //   Toggle the input pins with the Poke tool (hand icon); the output pins show the result.
endmodule
